// Logisim project Adder_Subtractors.circ as structural Verilog: 4 circuits, main circuit logisim16A_S
module logisim16A_S (
  input  [15:0] a,
  input  [15:0] b,
  input  OP,
  output [15:0] s,
  output overflow
);

  wire and_1_out, nand_1_out, nand_2_out, nor_1_out, nor_2_out, or_1_out;
  wire [15:0] multiplexer_1_out, not_1_out;

  Multiplexer #(.width(16)) multiplexer_1 (.in0(b), .in1(not_1_out), .out(multiplexer_1_out), .sel(OP));
  assign not_1_out = ~b;  // NOT_Gate not_1, 16 bits wide
  Adder #(.width(16)) adder_1 (.a(a), .b(multiplexer_1_out), .out(s), .cin(OP));  // open: cout
  and and_1 (and_1_out, a[15], multiplexer_1_out[15]);
  nor nor_1 (nor_1_out, a[15], multiplexer_1_out[15]);
  nand nand_1 (nand_1_out, a[15], s[15]);
  or or_1 (or_1_out, a[15], s[15]);
  nor nor_2 (nor_2_out, and_1_out, nor_1_out);
  nand nand_2 (nand_2_out, nand_1_out, or_1_out);
  nor nor_3 (overflow, nor_2_out, nand_2_out);
endmodule

module my16A_S (
  input  [15:0] a,
  input  [15:0] b,
  input  OP,
  output [15:0] s,
  output overflow
);

  wire and_1_out, nand_1_out, nand_2_out, nor_1_out, nor_2_out, or_1_out;
  wire [15:0] multiplexer_1_out, not_1_out;

  Multiplexer #(.width(16)) multiplexer_1 (.in0(b), .in1(not_1_out), .out(multiplexer_1_out), .sel(OP));
  assign not_1_out = ~b;  // NOT_Gate not_1, 16 bits wide
  CSA16_cin csa16_cin_1 (.a(a), .b(multiplexer_1_out), .cin(OP), .s(s));
  and and_1 (and_1_out, a[15], multiplexer_1_out[15]);
  nor nor_1 (nor_1_out, a[15], multiplexer_1_out[15]);
  nand nand_1 (nand_1_out, a[15], s[15]);
  or or_1 (or_1_out, a[15], s[15]);
  nor nor_2 (nor_2_out, and_1_out, nor_1_out);
  nand nand_2 (nand_2_out, nand_1_out, or_1_out);
  nor nor_3 (overflow, nor_2_out, nand_2_out);
endmodule

module CSA16_cin (
  input  [15:0] a,
  input  [15:0] b,
  input  cin,
  output [15:0] s
);

  wire csa8_0_2_cout, csa8_1_2_cout, multiplexer_1_out;
  wire [7:0] csa8_0_1_s, csa8_0_2_s, csa8_1_1_s, csa8_1_2_s, mx2i_8_1_z;

  CSA8_1 csa8_1_1 (.a(a[15:8]), .b(b[15:8]), .s(csa8_1_1_s));  // open: cout
  CSA8_0 csa8_0_1 (.a(a[15:8]), .b(b[15:8]), .s(csa8_0_1_s));  // open: cout
  mx2i_8 mx2i_8_1 (.s(multiplexer_1_out), .in0(csa8_0_1_s), .in1(csa8_1_1_s), .z(mx2i_8_1_z));
  Multiplexer multiplexer_1 (.in0(csa8_0_2_cout), .in1(csa8_1_2_cout), .out(multiplexer_1_out), .sel(cin));
  assign s[15:8] = ~mx2i_8_1_z;  // NOT_Gate not_1, 8 bits wide
  CSA8_0 csa8_0_2 (.a(a[7:0]), .b(b[7:0]), .cout(csa8_0_2_cout), .s(csa8_0_2_s));
  Multiplexer #(.width(8)) multiplexer_2 (.in0(csa8_0_2_s), .in1(csa8_1_2_s), .out(s[7:0]), .sel(cin));
  CSA8_1 csa8_1_2 (.a(a[7:0]), .b(b[7:0]), .cout(csa8_1_2_cout), .s(csa8_1_2_s));
endmodule

module overflow (
  input  A3,
  input  B3,
  input  OP,
  input  R3,
  output overflo
);

  wire and_1_out, multiplexer_1_out, nand_1_out, nand_2_out, nor_1_out, nor_2_out, not_1_out, or_1_out;

  Multiplexer multiplexer_1 (.in0(B3), .in1(not_1_out), .out(multiplexer_1_out), .sel(OP));
  not not_1 (not_1_out, B3);
  and and_1 (and_1_out, A3, multiplexer_1_out);
  nor nor_1 (nor_1_out, A3, multiplexer_1_out);
  nand nand_1 (nand_1_out, A3, R3);
  or or_1 (or_1_out, A3, R3);
  nor nor_2 (nor_2_out, and_1_out, nor_1_out);
  nand nand_2 (nand_2_out, nand_1_out, or_1_out);
  nor nor_3 (overflo, nor_2_out, nand_2_out);
endmodule
