// Logisim project Full_Adders.circ as structural Verilog: 12 circuits, main circuit FA0
module FA0 (
  input  a,
  input  b,
  output s,
  output cout
);

  wire nor_1_out;

  nor nor_1 (nor_1_out, a, b);
  and and_1 (cout, b, a);
  nor nor_2 (s, nor_1_out, cout);

  // Notes on the sheet:
  //   14 Transistors
  //   1.75
  //   FA0
  //   2.75
  //   Malcolmb Roalson
endmodule

module FA1 (
  input  a,
  input  b,
  output cout,
  output s
);

  wire nand_1_out;

  or or_1 (cout, a, b);
  nand nand_1 (nand_1_out, b, a);
  nand nand_2 (s, cout, nand_1_out);

  // Notes on the sheet:
  //   14 Transistors
  //   1.75
  //   FA1
  //   2.75
  //   Malcolmb Roalson
endmodule

module FAopt1 (
  input  a,
  input  b,
  input  cin,
  output s,
  output cout
);

  wire nand_1_out, nand_2_out, nor_1_out, nor_2_out, nor_3_out, not_1_out, not_2_out;

  nor nor_1 (nor_1_out, a, b);
  not not_1 (not_1_out, nand_1_out);
  nand nand_1 (nand_1_out, b, a);
  nor nor_2 (nor_2_out, nor_1_out, not_1_out);
  nor nor_3 (nor_3_out, nor_2_out, cin);
  not not_2 (not_2_out, nand_2_out);
  nand nand_2 (nand_2_out, nor_2_out, cin);
  nor nor_4 (s, nor_3_out, not_2_out);
  nand nand_3 (cout, nand_2_out, nand_1_out);

  // Notes on the sheet:
  //   32 Transistors
  //   FAopt1
  //   Malcolmb Roalson
  //   if Cin < 2.75 then 5.5 else Cin+2.75
  //   if Cin < 2.75 then 4.75 else Cin+2
endmodule

module FAopt2 (
  input  a,
  input  b,
  input  cin,
  output s,
  output cout
);

  wire and_1_out, nand_1_out, nand_2_out, nand_3_out, nor_1_out, nor_2_out, nor_3_out, not_1_out;

  nor nor_1 (nor_1_out, a, b);
  not not_1 (not_1_out, nand_1_out);
  nand nand_1 (nand_1_out, a, b);
  nand nand_2 (nand_2_out, b, cin);
  nand nand_3 (nand_3_out, cin, a);
  nor nor_2 (nor_2_out, nor_1_out, not_1_out);
  nand nand_4 (cout, nand_1_out, nand_2_out, nand_3_out);
  nor nor_3 (nor_3_out, nor_2_out, cin);
  and and_1 (and_1_out, nor_2_out, cin);
  nor nor_4 (s, nor_3_out, and_1_out);

  // Notes on the sheet:
  //   42 Transistors
  //   FAopt2
  //   Malcolmb Roalson
  //   Cin+2.25
  //   if Cin < 2.75 then 5.5 else Cin+2.75
endmodule

module Ripple4_0 (
  input  [3:0] a,
  input  [3:0] b,
  output [3:0] s,
  output cout
);

  wire fa0_1_cout, faopt1_1_cout, faopt2_1_cout;

  FA0 fa0_1 (.a(b[0]), .b(a[0]), .cout(fa0_1_cout), .s(s[0]));
  FAopt2 faopt2_1 (.a(b[1]), .b(a[1]), .cin(fa0_1_cout), .cout(faopt2_1_cout), .s(s[1]));
  FAopt1 faopt1_1 (.a(b[2]), .b(a[2]), .cin(faopt2_1_cout), .s(s[2]), .cout(faopt1_1_cout));
  FAopt1 faopt1_2 (.a(b[3]), .b(a[3]), .cin(faopt1_1_cout), .s(s[3]), .cout(cout));

  // Notes on the sheet:
  //   120 Transistors
  //   8.0
  //   4-bit Ripple
  //   Malcolmb Roalson
  //   8.75
endmodule

module Ripple8_0 (
  input  [7:0] a,
  input  [7:0] b,
  output [7:0] s,
  output cout
);

  wire fa0_1_cout, faopt1_1_cout, faopt1_2_cout, faopt1_3_cout, faopt1_4_cout, faopt1_5_cout, faopt2_1_cout;

  FA0 fa0_1 (.a(b[0]), .b(a[0]), .cout(fa0_1_cout), .s(s[0]));
  FAopt2 faopt2_1 (.a(b[1]), .b(a[1]), .cin(fa0_1_cout), .cout(faopt2_1_cout), .s(s[1]));
  FAopt1 faopt1_1 (.a(b[2]), .b(a[2]), .cin(faopt2_1_cout), .s(s[2]), .cout(faopt1_1_cout));
  FAopt1 faopt1_2 (.a(b[3]), .b(a[3]), .cin(faopt1_1_cout), .s(s[3]), .cout(faopt1_2_cout));
  FAopt1 faopt1_3 (.a(b[4]), .b(a[4]), .cin(faopt1_2_cout), .s(s[4]), .cout(faopt1_3_cout));
  FAopt1 faopt1_4 (.a(b[5]), .b(a[5]), .cin(faopt1_3_cout), .s(s[5]), .cout(faopt1_4_cout));
  FAopt1 faopt1_5 (.a(b[6]), .b(a[6]), .cin(faopt1_4_cout), .s(s[6]), .cout(faopt1_5_cout));
  FAopt1 faopt1_6 (.a(b[7]), .b(a[7]), .cin(faopt1_5_cout), .s(s[7]), .cout(cout));

  // Notes on the sheet:
  //   248 Transistors
  //   16.0
  //   8-bit Ripple
  //   Malcolmb Roalson
  //   16.75
endmodule

module Ripple4_1 (
  input  [3:0] a,
  input  [3:0] b,
  output [3:0] s,
  output cout
);

  wire fa1_1_cout, faopt1_1_cout, faopt2_1_cout;

  FA1 fa1_1 (.a(b[0]), .b(a[0]), .cout(fa1_1_cout), .s(s[0]));
  FAopt2 faopt2_1 (.a(b[1]), .b(a[1]), .cin(fa1_1_cout), .cout(faopt2_1_cout), .s(s[1]));
  FAopt1 faopt1_1 (.a(b[2]), .b(a[2]), .cin(faopt2_1_cout), .s(s[2]), .cout(faopt1_1_cout));
  FAopt1 faopt1_2 (.a(b[3]), .b(a[3]), .cin(faopt1_1_cout), .s(s[3]), .cout(cout));

  // Notes on the sheet:
  //   120 Transistors
  //   8.0
  //   4-bit Ripple
  //   Malcolmb Roalson
  //   8.75
endmodule

module CSA8_0 (
  input  [7:0] a,
  input  [7:0] b,
  output [7:0] s,
  output cout
);

  wire mx2i_2_1_z, ripple4_0_1_cout, ripple4_0_2_cout, ripple4_1_1_cout;
  wire [3:0] mx2i_4_1_z, ripple4_0_1_s, ripple4_1_1_s;

  Ripple4_1 ripple4_1_1 (.b(b[7:4]), .a(a[7:4]), .s(ripple4_1_1_s), .cout(ripple4_1_1_cout));
  Ripple4_0 ripple4_0_1 (.b(b[7:4]), .a(a[7:4]), .s(ripple4_0_1_s), .cout(ripple4_0_1_cout));
  mx2i_4 mx2i_4_1 (.s(ripple4_0_2_cout), .in0(ripple4_0_1_s), .in1(ripple4_1_1_s), .z(mx2i_4_1_z));
  mx2i_2 mx2i_2_1 (.in0(ripple4_0_1_cout), .in1(ripple4_1_1_cout), .s(ripple4_0_2_cout), .z(mx2i_2_1_z));
  not not_1 (cout, mx2i_2_1_z);
  assign s[7:4] = ~mx2i_4_1_z;  // NOT_Gate not_2, 4 bits wide
  Ripple4_0 ripple4_0_2 (.b(b[3:0]), .a(a[3:0]), .s(s[3:0]), .cout(ripple4_0_2_cout));

  // Notes on the sheet:
  //   10.5
  //   8-bit Carry Select
  //   Malcolmb Roalson
  //   10.5
endmodule

module mx2i_4 (
  input  [3:0] in0,
  input  [3:0] in1,
  input  s,
  output [3:0] z
);

  mx2i_2 mx2i_2_1 (.in0(in0[0]), .in1(in1[0]), .s(s), .z(z[0]));
  mx2i_2 mx2i_2_2 (.in0(in0[1]), .in1(in1[1]), .s(s), .z(z[1]));
  mx2i_2 mx2i_2_3 (.in0(in0[2]), .in1(in1[2]), .s(s), .z(z[2]));
  mx2i_2 mx2i_2_4 (.in0(in0[3]), .in1(in1[3]), .s(s), .z(z[3]));
endmodule

module CSA16 (
  input  [15:0] a,
  input  [15:0] b,
  output [15:0] s,
  output cout
);

  wire csa8_0_1_cout, csa8_0_2_cout, csa8_1_1_cout, mx2i_2_1_z;
  wire [7:0] csa8_0_1_s, csa8_1_1_s, mx2i_8_1_z;

  CSA8_1 csa8_1_1 (.a(a[15:8]), .b(b[15:8]), .cout(csa8_1_1_cout), .s(csa8_1_1_s));
  CSA8_0 csa8_0_1 (.a(a[15:8]), .b(b[15:8]), .cout(csa8_0_1_cout), .s(csa8_0_1_s));
  mx2i_8 mx2i_8_1 (.s(csa8_0_2_cout), .in0(csa8_0_1_s), .in1(csa8_1_1_s), .z(mx2i_8_1_z));
  mx2i_2 mx2i_2_1 (.in0(csa8_0_1_cout), .in1(csa8_1_1_cout), .s(csa8_0_2_cout), .z(mx2i_2_1_z));
  not not_1 (cout, mx2i_2_1_z);
  assign s[15:8] = ~mx2i_8_1_z;  // NOT_Gate not_2, 8 bits wide
  CSA8_0 csa8_0_2 (.a(a[7:0]), .b(b[7:0]), .cout(csa8_0_2_cout), .s(s[7:0]));

  // Notes on the sheet:
  //   13
  //   16-bit Carry Select
  //   Malcolmb Roalson
  //   13
endmodule

module CSA8_1 (
  input  [7:0] a,
  input  [7:0] b,
  output [7:0] s,
  output cout
);

  wire mx2i_2_1_z, ripple4_0_1_cout, ripple4_1_1_cout, ripple4_1_2_cout;
  wire [3:0] mx2i_4_1_z, ripple4_0_1_s, ripple4_1_1_s;

  Ripple4_1 ripple4_1_1 (.b(b[7:4]), .a(a[7:4]), .s(ripple4_1_1_s), .cout(ripple4_1_1_cout));
  Ripple4_0 ripple4_0_1 (.b(b[7:4]), .a(a[7:4]), .s(ripple4_0_1_s), .cout(ripple4_0_1_cout));
  mx2i_4 mx2i_4_1 (.s(ripple4_1_2_cout), .in0(ripple4_0_1_s), .in1(ripple4_1_1_s), .z(mx2i_4_1_z));
  mx2i_2 mx2i_2_1 (.in0(ripple4_0_1_cout), .in1(ripple4_1_1_cout), .s(ripple4_1_2_cout), .z(mx2i_2_1_z));
  not not_1 (cout, mx2i_2_1_z);
  assign s[7:4] = ~mx2i_4_1_z;  // NOT_Gate not_2, 4 bits wide
  Ripple4_1 ripple4_1_2 (.b(b[3:0]), .a(a[3:0]), .s(s[3:0]), .cout(ripple4_1_2_cout));

  // Notes on the sheet:
  //   10.5
  //   8-bit Carry Select
  //   Malcolmb Roalson
  //   10.5
endmodule

module mx2i_8 (
  input  [7:0] in0,
  input  [7:0] in1,
  input  s,
  output [7:0] z
);

  mx2i_4 mx2i_4_1 (.s(s), .in0(in0[3:0]), .in1(in1[3:0]), .z(z[3:0]));
  mx2i_4 mx2i_4_2 (.s(s), .in0(in0[7:4]), .in1(in1[7:4]), .z(z[7:4]));
endmodule
