// Logisim project LALU_2.0.circ as structural Verilog: 17 circuits, main circuit main
module main (
  input  bclk,
  input  rst,
  input  run,
  input  CLK_50,
  input  [3:0] dispReg,
  input  PS2_CLK,
  input  PS2_DAT,
  input  dispCyc,
  input  dispIR,
  input  dispPC,
  output VGA_VS,
  output VGA_HS,
  output VGA_BLANK_N,
  output VGA_SYNC_N,
  output VGA_CLK,
  output [7:0] VGA_B,
  output [7:0] VGA_G,
  output [7:0] VGA_R
);

  wire add, adderOvfl, altiJmp, altJmp, and_2_out, and_3_out, and_4_out, and_5_out, and_11_out, and_12_out,
       and_13_out, and_14_out, and_15_out, and_16_out, and_17_out, and_18_out, and_19_out, and_20_out,
       and_21_out, and_22_out, and_23_out, and_24_out, and_26_out, and_27_out, and_39_out, and_40_out,
       and_41_out, and_42_out, and_43_out, and_44_out, and_45_out, and_46_out, and_47_out, and_48_out,
       and_49_out, and_50_out, and_51_out, and_52_out, and_53_out, and_54_out, and_55_out, and_56_out,
       and_57_out, and_58_out, and_59_out, and_60_out, and_61_out, and_62_out, and_63_out, and_64_out,
       and_65_out, and_66_out, and_67_out, and_68_out, and_69_out, and_70_out, and_71_out, and_72_out,
       and_73_out, and_74_out, and_75_out, and_76_out, and_77_out, and_78_out, and_79_out, and_80_out,
       and_81_out, and_82_out, and_84_out, and_85_out, and_86_out, and_87_out, and_88_out, and_89_out,
       and_90_out, and_91_out, and_93_out, and_94_out, and_95_out, and_96_out, and_97_out, and_98_out,
       and_99_out, and_100_out, and_101_out, and_102_out, and_103_out, and_104_out, and_105_out, and_106_out,
       any, bAnd, bOr, bs, bsl, bsOob, bsRot, bXor, call, callExec, checkMask4_2_valid, checkMask16_1_valid,
       checkMask16_2_valid, checkMask16_3_valid, clk, clk_out, d_ff_1_q, d_ff_1_qn, d_ff_2_qn, d_ff_3_qn,
       d_ff_4_q, dataFlags_1_neg, dataFlags_1_nz, dataFlags_1_zero, dataFlags_2_neg, dataFlags_2_odd,
       dataFlags_2_zero, enpr, enprExec, enprExecIR, enprIR, exJmp, expr, exprExec, freeze, frozen, halt,
       haltIR, hsb, iFlag, iJmp, isSignedMul, jmp, jmpAbs, jmpfault, jmpPC, jmpPCFin, jumped, ld, ldIR,
       ldkey, ldkeyp, ldkeyr, lfm, lfmz, mapOut, memFrz, memOp, mul, mulOvfl, multiplexer_1_out,
       multiplexer_8_out, multiplexer_48_out, multiplexer_74_out, multiplexer_82_out, mv, nand_1_out,
       nand_2_out, nand_3_out, nor_1_out, not_2_out, not_3_out, or_2_out, or_3_out, or_8_out, or_9_out,
       or_10_out, or_11_out, or_13_out, or_15_out, or_16_out, or_17_out, or_18_out, or_19_out, or_20_out,
       or_21_out, or_22_out, or_26_out, or_27_out, or_28_out, or_29_out, or_30_out, or_31_out, or_32_out,
       or_33_out, or_34_out, or_35_out, or_36_out, or_37_out, or_38_out, or_39_out, or_40_out, or_41_out,
       or_42_out, or_43_out, or_44_out, or_45_out, or_47_out, or_48_out, or_50_out, or_52_out, or_53_out,
       or_54_out, or_55_out, or_56_out, or_57_out, or_58_out, or_59_out, ovfl, par, parExec, parExecIR,
       parIR, pop, popIR, popStk, popStkExec, prhdl, prhdlIR, prmem, prmemIR, \protected , prprg, prprgIR,
       prreg, prregIR, pshStk, pshStkExec, push, register_1_q, register_22_q, register_24_q, ret, retExec,
       retExecIR, retIR, rstkey, sar, sarExec, segfault, st, stalled, stchr, stIR, stkPopAllowed, sub, unfl,
       useAdder, usm, usmz, utilFlag, validRdRe, validRdWr, validRsRe, we;
  wire [0:0] or_49_out;
  wire [2:0] jmpFlags;
  wire [3:0] multiplexer_11_out, multiplexer_11_out_2, multiplexer_11_out_3, multiplexer_11_out_4,
       multiplexer_39_out, multiplexer_40_out, multiplexer_54_out, multiplexer_55_out, prRegReMask,
       prRegReValue, prRegWrMask, prRegWrValue, Rd, Rj, Rs, xor_2_out;
  wire [6:0] multiplexer_45_out;
  wire [6:6] multiplexer_38_out;
  wire [7:0] altImmJmp, keyBuffer, multiplexer_50_out, printKey;
  wire [8:0] dataIn, immJmp;
  wire [15:0] adder_1_out, and_92_out, bitShift_1_shifted, cycles, data, dataRd, dataRj, dataRs,
       earlyLitStkPtr, earlyStackPtr, enprFramePtr, enprFrmPtr, enprRetVal, framePtr, freezeReg16_1_q,
       freezeReg16_2_q, freezeReg16_4_q, highestSetBit_1_hsb, IR, ldData, litStkPtr, logisim16A_S_1_s,
       mul16_1_ab, multiplexer_2_out, multiplexer_3_out, multiplexer_4_out, multiplexer_5_out,
       multiplexer_6_out, multiplexer_7_out, multiplexer_9_out, multiplexer_10_out, multiplexer_12_out,
       multiplexer_13_out, multiplexer_14_out, multiplexer_15_out, multiplexer_16_out, multiplexer_17_out,
       multiplexer_18_out, multiplexer_19_out, multiplexer_20_out, multiplexer_21_out, multiplexer_22_out,
       multiplexer_23_out, multiplexer_24_out, multiplexer_25_out, multiplexer_26_out, multiplexer_27_out,
       multiplexer_28_out, multiplexer_29_out, multiplexer_30_out, multiplexer_32_out, multiplexer_33_out,
       multiplexer_37_out, multiplexer_41_out, multiplexer_42_out, multiplexer_43_out, multiplexer_44_out,
       multiplexer_46_out, multiplexer_49_out, multiplexer_51_out, multiplexer_52_out, multiplexer_53_out,
       multiplexer_56_out, multiplexer_57_out, multiplexer_58_out, multiplexer_59_out, multiplexer_60_out,
       multiplexer_61_out, multiplexer_62_out, multiplexer_63_out, multiplexer_65_out, multiplexer_66_out,
       multiplexer_67_out, multiplexer_68_out, multiplexer_69_out, multiplexer_70_out, multiplexer_71_out,
       multiplexer_73_out, multiplexer_75_out, multiplexer_76_out, multiplexer_77_out, multiplexer_78_out,
       multiplexer_79_out, multiplexer_80_out, multiplexer_83_out, multiplexer_84_out, multiplexer_85_out,
       multiplexer_86_out, multiplexer_87_out, not_1_out, opc, or_51_out, PC, prHdlLoc, prMemReMask,
       prMemReValue, prMemWrMask, prMemWrValue, prPrgReMask, prPrgReValue, prPrgWrMask, prPrgWrValue,
       RAM_1_dout, rawKey, Rdisp, register_2_q, register_5_q, register_6_q, register_7_q, register_8_q,
       register_9_q, register_10_q, register_11_q, register_12_q, register_13_q, register_14_q,
       register_15_q, register_16_q, register_17_q, register_18_q, register_19_q, register_20_q, regRs,
       retVal, sarFrmPtr, sarRetVal, stackPtr, xor_1_out, xor_3_out, xor_4_out;

  Register #(.width(1)) register_1 (.D(1'b1), .en(halt), .clk(clk), .Q(register_1_q), .clr(rst));
  Clock u_clk (.out(clk_out));
  or or_1 (useAdder, add, sub);
  Multiplexer multiplexer_1 (.in0(bclk), .in1(clk_out), .out(multiplexer_1_out), .sel(run));
  LED clkLED (.in(clk));
  and and_1 (clk, ~register_1_q, d_ff_1_q, multiplexer_1_out);  // AND_Gate
  D_Flip_Flop #(.trigger("falling")) d_ff_1 (
    .D(1'b1), .clk(multiplexer_1_out), .Q(d_ff_1_q), .Qn(d_ff_1_qn), .reset(rst));  // open: preset
  assign xor_1_out = framePtr ^ litStkPtr;  // XOR_Gate xor_1, 16 bits wide
  nand nand_1 (nand_1_out, validRdWr, validRsRe, validRdRe);
  cycleCounter cycleCounter_1 (.clk(clk), .rst(rst), .freeze(freeze), .cycles(cycles));
  or or_2 (or_2_out, st, pshStkExec, push);
  and and_2 (and_2_out, or_2_out, ~segfault);  // AND_Gate
  or or_3 (or_3_out, ld, popStkExec, pop);
  and and_3 (and_3_out, or_3_out, ~segfault);  // AND_Gate
  or or_4 (pshStk, call, enpr, sar);
  or or_5 (pshStkExec, callExec, enprExec, sarExec);
  or or_6 (popStk, ret, expr, par);
  or or_7 (popStkExec, retExec, exprExec, parExec);
  and and_4 (and_4_out, nand_1_out, or_8_out);
  or or_8 (or_8_out, add, sub, mul, bs, bAnd, lfmz, lfm, bXor, bOr);
  and and_5 (and_5_out, popStkExec, frozen);
  Multiplexer #(.width(16)) multiplexer_2 (.in0(PC), .in1(framePtr), .out(multiplexer_2_out), .sel(frozen));
  or or_9 (or_9_out, xor_1_out[0], xor_1_out[1], xor_1_out[2], xor_1_out[3], xor_1_out[4], xor_1_out[5], xor_1_out[6], xor_1_out[7], xor_1_out[8], xor_1_out[9], xor_1_out[10], xor_1_out[11], xor_1_out[12], xor_1_out[13], xor_1_out[14], xor_1_out[15]);
  nand nand_2 (nand_2_out, validRdWr, validRsRe);
  or or_10 (or_10_out, jmpAbs, popStk, pshStk);
  or or_11 (or_11_out, popStkExec, pop);
  or or_12 (memOp, and_3_out, and_2_out);
  Multiplexer #(.width(16)) multiplexer_3 (
    .in0(dataRd), .in1(multiplexer_2_out), .out(multiplexer_3_out), .sel(pshStkExec));
  and and_6 (retExec, retExecIR, or_13_out);
  or or_13 (or_13_out, frozen, stkPopAllowed);
  and and_7 (ret, retIR, stkPopAllowed);
  and and_8 (pop, popIR, or_9_out);
  and and_9 (ld, ldIR, checkMask16_1_valid);
  checkMask16 checkMask16_1 (
    .mask(prMemReMask), .value(dataRs), .targVal(prMemReValue), .prot(\protected ),
    .valid(checkMask16_1_valid));
  and and_10 (st, stIR, checkMask16_3_valid);
  checkMask16 checkMask16_3 (
    .mask(prMemWrMask), .value(dataRs), .targVal(prMemWrValue), .prot(\protected ),
    .valid(checkMask16_3_valid));
  or or_14 (validRsRe, iFlag, checkMask4_2_valid);
  checkMask4 checkMask4_2 (
    .mask(prRegReMask), .value(Rs), .targVal(prRegReValue), .prot(\protected ), .valid(checkMask4_2_valid));
  and and_11 (and_11_out, nand_2_out, or_15_out);
  or or_15 (or_15_out, ld, hsb, mv, any);
  Multiplexer #(.width(16)) multiplexer_4 (.in0(data), .in1(register_2_q), .out(multiplexer_4_out), .sel(memFrz));
  Register #(.width(16)) register_2 (.D(multiplexer_4_out), .en(1'b1), .clk(clk), .Q(register_2_q), .clr(rst));
  dataFlags dataFlags_2 (
    .data(data), .odd(dataFlags_2_odd), .zero(dataFlags_2_zero), .neg(dataFlags_2_neg));  // open: nz
  assign not_1_out = ~framePtr;  // NOT_Gate not_1, 16 bits wide
  Multiplexer #(.width(16)) multiplexer_5 (
    .in0(earlyStackPtr), .in1(adder_1_out), .out(multiplexer_5_out), .sel(and_5_out));
  Multiplexer #(.width(16)) multiplexer_6 (
    .in0(stackPtr), .in1(multiplexer_5_out), .out(multiplexer_6_out), .sel(or_11_out));
  or or_16 (or_16_out, st, ld);
  Multiplexer #(.width(16)) multiplexer_7 (
    .in0(multiplexer_6_out), .in1(dataRs), .out(multiplexer_7_out), .sel(or_16_out));
  RAM #(.addrWidth(16), .dataWidth(16), .trigger("falling")) RAM_2 (
    .addr(multiplexer_7_out), .we(and_2_out), .oe(and_3_out), .clk(clk), .din(multiplexer_3_out),
    .dout(ldData));
  and and_12 (and_12_out, nand_3_out, st);
  nand nand_3 (nand_3_out, validRsRe, validRdRe);
  Adder #(.width(16)) adder_1 (.a(not_1_out), .b(16'h2), .out(adder_1_out));  // open: cin, cout
  and and_13 (and_13_out, ~validRdWr, pop);  // AND_Gate
  or or_17 (or_17_out, bs, mv, ld, bAnd, any, useAdder, bXor, bOr, lfm, lfmz, mul, pop, ldkey);
  and and_14 (and_14_out, \protected , ~or_18_out);  // AND_Gate
  or or_18 (or_18_out, expr, sar);
  and and_15 (and_15_out, ~validRsRe, or_19_out);  // AND_Gate
  or or_19 (or_19_out, push, and_16_out, usmz, usm);
  and and_16 (and_16_out, jmp, ~iJmp);  // AND_Gate
  and and_17 (and_17_out, ~jmpFlags[0], ~jmpFlags[1], ~jmpFlags[2]);  // AND_Gate
  and and_18 (and_18_out, dataFlags_2_neg, jmpFlags[0], ~jmpFlags[1], ~jmpFlags[2]);  // AND_Gate
  and and_19 (and_19_out, dataFlags_2_zero, ~jmpFlags[0], jmpFlags[1], ~jmpFlags[2]);  // AND_Gate
  and and_20 (and_20_out, ovfl, jmpFlags[0], jmpFlags[1], ~jmpFlags[2]);  // AND_Gate
  and and_21 (and_21_out, unfl, ~jmpFlags[0], ~jmpFlags[1], jmpFlags[2]);  // AND_Gate
  and and_22 (and_22_out, dataFlags_2_odd, jmpFlags[0], ~jmpFlags[1], jmpFlags[2]);  // AND_Gate
  and and_23 (and_23_out, utilFlag, ~jmpFlags[0], jmpFlags[1], jmpFlags[2]);  // AND_Gate
  and and_24 (and_24_out, ~utilFlag, jmpFlags[0], jmpFlags[1], jmpFlags[2]);  // AND_Gate
  programCounter programCounter_1 (
    .jmpVal(dataRj), .jmp(jmpPCFin), .jmpAbs(or_10_out), .clk(clk), .rst(rst), .freeze(freeze), .pc(opc));
  or or_20 (or_20_out, d_ff_1_qn, clk);
  and and_25 (we, ~segfault, or_17_out);  // AND_Gate
  dataFlags dataFlags_1 (
    .data(register_2_q), .nz(dataFlags_1_nz), .zero(dataFlags_1_zero), .neg(dataFlags_1_neg));  // open: odd
  RAM #(.addrWidth(16), .dataWidth(16), .trigger("falling")) RAM_1 (
    .addr(opc), .we(1'b0), .oe(1'b1), .clk(or_20_out), .dout(RAM_1_dout));  // open: din
  Multiplexer multiplexer_8 (.in0(dataFlags_1_nz), .in1(dataFlags_1_zero), .out(multiplexer_8_out), .sel(or_21_out));
  freezeReg16 freezeReg16_2 (.freeze(freeze), .D(opc), .WE(1'b1), .clk(clk), .R(rst), .Q(freezeReg16_2_q));
  not not_2 (not_2_out, \protected );
  checkMask16 checkMask16_2 (
    .mask(prPrgReMask), .value(dataRj), .targVal(prPrgReValue), .prot(and_14_out), .valid(checkMask16_2_valid));
  checkMask4 checkMask4_1 (
    .mask(prRegReMask), .value(Rd), .targVal(prRegReValue), .prot(\protected ), .valid(validRdRe));
  checkMask4 checkMask4_3 (
    .mask(prRegWrMask), .value(Rd), .targVal(prRegWrValue), .prot(\protected ), .valid(validRdWr));
  and and_26 (and_26_out, ldIR, ~ld);  // AND_Gate
  and and_27 (and_27_out, stIR, ~st);  // AND_Gate
  and and_28 (jmpfault, jmpPC, ~jmpPCFin);  // AND_Gate
  LED jmpfaultLED (.in(jmpfault));
  or or_21 (or_21_out, lfmz, usmz);
  or or_22 (or_22_out, and_17_out, and_18_out, and_19_out, and_20_out, and_21_out, and_22_out, and_23_out, and_24_out);
  and and_29 (par, parIR, not_2_out);
  and and_30 (enpr, enprIR, not_2_out);
  and and_31 (prreg, prregIR, not_2_out);
  and and_32 (prmem, prmemIR, not_2_out);
  and and_33 (prprg, prprgIR, not_2_out);
  and and_34 (enprExec, enprExecIR, not_2_out);
  and and_35 (parExec, parExecIR, not_2_out);
  and and_36 (prhdl, prhdlIR, not_2_out);
  and and_37 (halt, haltIR, not_2_out);
  and and_38 (jmpPCFin, jmpPC, checkMask16_2_valid);
  freezeReg freezeReg_2 (.freeze(freeze), .D(jmpPCFin), .we(1'b1), .clk(clk), .R(rst), .Q(jumped));
  or or_23 (segfault, and_11_out, and_4_out, and_13_out, and_15_out, and_26_out, and_27_out, and_12_out);
  and and_39 (and_39_out, jmp, or_22_out);
  freezeReg16 freezeReg16_3 (.freeze(freeze), .D(freezeReg16_2_q), .WE(1'b1), .clk(clk), .R(rst), .Q(PC));
  LED segfaultLED (.in(segfault));
  and and_40 (and_40_out, dataRs[3], multiplexer_8_out);
  and and_41 (and_41_out, dataRs[2], dataFlags_1_neg);
  or or_24 (jmpPC, sar, par, call, and_39_out, ret, enpr, expr);
  Multiplexer #(.width(16)) multiplexer_9 (.in0(Rdisp), .in1(cycles), .out(multiplexer_9_out), .sel(dispCyc));
  and and_42 (and_42_out, dataRs[1], ovfl);
  Hex_Digit_Display #(.decimalPoint("false")) c3 (.value(multiplexer_11_out_4));
  Hex_Digit_Display #(.decimalPoint("false")) c2 (.value(multiplexer_11_out_3));
  Multiplexer #(.width(16)) multiplexer_10 (.in0(multiplexer_9_out), .in1(IR), .out(multiplexer_10_out), .sel(dispIR));
  Register #(.width(16)) register_3 (.clk(clk), .clr(rst));  // open: D, en, Q
  and and_43 (and_43_out, dataRs[0], unfl);
  Hex_Digit_Display #(.decimalPoint("false")) c1 (.value(multiplexer_11_out_2));
  Hex_Digit_Display #(.decimalPoint("false")) c0 (.value(multiplexer_11_out));
  Multiplexer #(.width(16)) multiplexer_11 (
    .in0(multiplexer_10_out), .in1(opc),
    .out({multiplexer_11_out_4, multiplexer_11_out_3, multiplexer_11_out_2, multiplexer_11_out}), .sel(dispPC));
  freezeReg16 freezeReg16_1 (.freeze(stalled), .D(RAM_1_dout), .WE(freeze), .clk(clk), .R(rst), .Q(freezeReg16_1_q));
  IRDecoder IRDecoder_1 (
    .clk(clk), .rst(rst), .freeze(freeze), .IR(IR), .dataIn(dataIn), .Rs(Rs), .Rd(Rd), .i(iFlag), .add(add),
    .sub(sub), .ld(ldIR), .mv(mv), .st(stIR), .halt(haltIR), .bs(bs), .bsLeft(bsl), .bsRot(bsRot),
    .bAnd(bAnd), .bOr(bOr), .bXor(bXor), .any(any), .lfm(lfm), .lfmz(lfmz), .usm(usm), .usmz(usmz),
    .hsb(hsb), .exJmp(exJmp), .call(callExec), .ret(retExecIR), .isSignedMul(isSignedMul), .mul(mul),
    .push(push), .pop(popIR), .prreg(prregIR), .prmem(prmemIR), .prprg(prprgIR), .enpr(enprExecIR),
    .expr(exprExec), .sar(sarExec), .par(parExecIR), .ldkeyr(ldkeyr), .stchr(stchr), .ldkeyp(ldkeyp),
    .rstkey(rstkey));  // open: nop
  or or_25 (mapOut, and_40_out, and_41_out, and_42_out, and_43_out);
  Multiplexer #(.width(16)) multiplexer_12 (
    .in0(RAM_1_dout), .in1(freezeReg16_1_q), .out(multiplexer_12_out), .sel(stalled));
  Register #(.width(16)) register_4 (.D(multiplexer_13_out), .en(1'b1), .clk(clk), .Q(IR), .clr(or_27_out));
  Multiplexer #(.width(16)) multiplexer_13 (
    .in0(multiplexer_12_out), .in1(IR), .out(multiplexer_13_out), .sel(or_26_out));
  or or_26 (or_26_out, freeze, jumped);
  or or_27 (or_27_out, jumped, rst);
  and and_44 (and_44_out, ~Rd[0], ~Rd[1], ~Rd[2], ~Rd[3]);  // AND_Gate
  and and_45 (and_45_out, Rd[0], ~Rd[1], ~Rd[2], ~Rd[3]);  // AND_Gate
  and and_46 (and_46_out, ~Rd[0], Rd[1], ~Rd[2], ~Rd[3]);  // AND_Gate
  and and_47 (and_47_out, Rd[0], Rd[1], ~Rd[2], ~Rd[3]);  // AND_Gate
  and and_48 (and_48_out, ~Rd[0], ~Rd[1], Rd[2], ~Rd[3]);  // AND_Gate
  and and_49 (and_49_out, Rd[0], ~Rd[1], Rd[2], ~Rd[3]);  // AND_Gate
  and and_50 (and_50_out, ~Rd[0], Rd[1], Rd[2], ~Rd[3]);  // AND_Gate
  and and_51 (and_51_out, Rd[0], Rd[1], Rd[2], ~Rd[3]);  // AND_Gate
  and and_52 (and_52_out, ~Rd[0], ~Rd[1], ~Rd[2], Rd[3]);  // AND_Gate
  and and_53 (and_53_out, Rd[0], ~Rd[1], ~Rd[2], Rd[3]);  // AND_Gate
  and and_54 (and_54_out, ~Rd[0], Rd[1], ~Rd[2], Rd[3]);  // AND_Gate
  and and_55 (and_55_out, Rd[0], Rd[1], ~Rd[2], Rd[3]);  // AND_Gate
  and and_56 (and_56_out, ~Rd[0], ~Rd[1], Rd[2], Rd[3]);  // AND_Gate
  and and_57 (and_57_out, Rd[0], ~Rd[1], Rd[2], Rd[3]);  // AND_Gate
  and and_58 (and_58_out, ~Rd[0], Rd[1], Rd[2], Rd[3]);  // AND_Gate
  and and_59 (and_59_out, Rd[0], Rd[1], Rd[2], Rd[3]);
  Multiplexer #(.width(16)) multiplexer_14 (.in0(data), .in1(register_5_q), .out(multiplexer_14_out), .sel(freeze));
  Register #(.width(16)) register_5 (.D(multiplexer_14_out), .en(and_60_out), .clk(clk), .Q(register_5_q), .clr(rst));
  and and_60 (and_60_out, and_44_out, we);
  Multiplexer #(.width(16)) multiplexer_15 (.in0(data), .in1(register_6_q), .out(multiplexer_15_out), .sel(freeze));
  Register #(.width(16)) register_6 (.D(multiplexer_15_out), .en(and_61_out), .clk(clk), .Q(register_6_q), .clr(rst));
  and and_61 (and_61_out, and_45_out, we);
  Multiplexer #(.width(16)) multiplexer_16 (.in0(data), .in1(register_7_q), .out(multiplexer_16_out), .sel(freeze));
  Register #(.width(16)) register_7 (.D(multiplexer_16_out), .en(and_62_out), .clk(clk), .Q(register_7_q), .clr(rst));
  and and_62 (and_62_out, and_46_out, we);
  Multiplexer #(.width(16)) multiplexer_17 (.in0(data), .in1(register_8_q), .out(multiplexer_17_out), .sel(freeze));
  Register #(.width(16)) register_8 (.D(multiplexer_17_out), .en(and_63_out), .clk(clk), .Q(register_8_q), .clr(rst));
  and and_63 (and_63_out, and_47_out, we);
  Multiplexer #(.width(16)) multiplexer_18 (.in0(data), .in1(register_9_q), .out(multiplexer_18_out), .sel(freeze));
  Register #(.width(16)) register_9 (.D(multiplexer_18_out), .en(and_64_out), .clk(clk), .Q(register_9_q), .clr(rst));
  and and_64 (and_64_out, and_48_out, we);
  Multiplexer #(.width(16)) multiplexer_19 (.in0(data), .in1(register_10_q), .out(multiplexer_19_out), .sel(freeze));
  Register #(.width(16)) register_10 (.D(multiplexer_19_out), .en(and_65_out), .clk(clk), .Q(register_10_q), .clr(rst));
  and and_65 (and_65_out, and_49_out, we);
  Multiplexer #(.width(16)) multiplexer_20 (.in0(data), .in1(register_11_q), .out(multiplexer_20_out), .sel(freeze));
  Register #(.width(16)) register_11 (.D(multiplexer_20_out), .en(and_66_out), .clk(clk), .Q(register_11_q), .clr(rst));
  and and_66 (and_66_out, and_50_out, we);
  Multiplexer #(.width(16)) multiplexer_21 (.in0(data), .in1(register_12_q), .out(multiplexer_21_out), .sel(freeze));
  Register #(.width(16)) register_12 (.D(multiplexer_21_out), .en(and_67_out), .clk(clk), .Q(register_12_q), .clr(rst));
  and and_67 (and_67_out, and_51_out, we);
  Multiplexer #(.width(16)) multiplexer_22 (.in0(data), .in1(register_13_q), .out(multiplexer_22_out), .sel(freeze));
  Register #(.width(16)) register_13 (.D(multiplexer_22_out), .en(and_68_out), .clk(clk), .Q(register_13_q), .clr(rst));
  and and_68 (and_68_out, and_52_out, we);
  Multiplexer #(.width(16)) multiplexer_23 (.in0(data), .in1(register_14_q), .out(multiplexer_23_out), .sel(freeze));
  Register #(.width(16)) register_14 (.D(multiplexer_23_out), .en(and_69_out), .clk(clk), .Q(register_14_q), .clr(rst));
  and and_69 (and_69_out, and_53_out, we);
  Multiplexer #(.width(16)) multiplexer_24 (.in0(data), .in1(register_15_q), .out(multiplexer_24_out), .sel(freeze));
  Register #(.width(16)) register_15 (.D(multiplexer_24_out), .en(and_70_out), .clk(clk), .Q(register_15_q), .clr(rst));
  and and_70 (and_70_out, and_54_out, we);
  Multiplexer #(.width(16)) multiplexer_25 (.in0(data), .in1(register_16_q), .out(multiplexer_25_out), .sel(freeze));
  Register #(.width(16)) register_16 (.D(multiplexer_25_out), .en(and_71_out), .clk(clk), .Q(register_16_q), .clr(rst));
  and and_71 (and_71_out, and_55_out, we);
  Multiplexer #(.width(16)) multiplexer_26 (.in0(data), .in1(register_17_q), .out(multiplexer_26_out), .sel(freeze));
  Register #(.width(16)) register_17 (.D(multiplexer_26_out), .en(and_72_out), .clk(clk), .Q(register_17_q), .clr(rst));
  and and_72 (and_72_out, and_56_out, we);
  Multiplexer #(.width(16)) multiplexer_27 (.in0(data), .in1(register_18_q), .out(multiplexer_27_out), .sel(freeze));
  Register #(.width(16)) register_18 (.D(multiplexer_27_out), .en(and_73_out), .clk(clk), .Q(register_18_q), .clr(rst));
  and and_73 (and_73_out, and_57_out, we);
  Multiplexer #(.width(16)) multiplexer_28 (.in0(data), .in1(register_19_q), .out(multiplexer_28_out), .sel(freeze));
  Register #(.width(16)) register_19 (.D(multiplexer_28_out), .en(and_74_out), .clk(clk), .Q(register_19_q), .clr(rst));
  and and_74 (and_74_out, and_58_out, we);
  Multiplexer #(.width(16)) multiplexer_29 (.in0(data), .in1(register_20_q), .out(multiplexer_29_out), .sel(freeze));
  Register #(.width(16)) register_20 (.D(multiplexer_29_out), .en(and_75_out), .clk(clk), .Q(register_20_q), .clr(rst));
  and and_75 (and_75_out, and_59_out, we);
  jumpDecoder jumpDecoder_1 (
    .IR(IR), .flags(jmpFlags), .absolute(jmpAbs), .jmp(jmp), .i(iJmp), .Rj(Rj), .immediate(immJmp),
    .alti(altiJmp), .altImm(altImmJmp), .call(call), .ret(retIR), .prhdl(prhdlIR), .altJmp(altJmp),
    .enpr(enprIR), .expr(expr), .sar(sar), .par(parIR));
  Multiplexer #(.select(4), .width(16)) multiplexer_30 (
    .in0(register_5_q), .in1(register_6_q), .in2(register_7_q), .in3(register_8_q), .in4(register_9_q),
    .in5(register_10_q), .in6(register_11_q), .in7(register_12_q), .in8(register_13_q), .in9(register_14_q),
    .in10(register_15_q), .in11(register_16_q), .in12(register_17_q), .in13(register_18_q),
    .in14(register_19_q), .in15(register_20_q), .out(multiplexer_30_out), .sel(Rd));
  Multiplexer #(.width(16)) multiplexer_31 (.in0({16{1'b0}}), .in1(multiplexer_32_out), .out(regRs), .sel(validRdRe));
  Multiplexer #(.select(4), .width(16)) multiplexer_32 (
    .in0(register_5_q), .in1(register_6_q), .in2(register_7_q), .in3(register_8_q), .in4(register_9_q),
    .in5(register_10_q), .in6(register_11_q), .in7(register_12_q), .in8(register_13_q), .in9(register_14_q),
    .in10(register_15_q), .in11(register_16_q), .in12(register_17_q), .in13(register_18_q),
    .in14(register_19_q), .in15(register_20_q), .out(multiplexer_32_out), .sel(Rs));
  Multiplexer #(.select(4), .width(16)) multiplexer_33 (
    .in0(register_5_q), .in1(register_6_q), .in2(register_7_q), .in3(register_8_q), .in4(register_9_q),
    .in5(register_10_q), .in6(register_11_q), .in7(register_12_q), .in8(register_13_q), .in9(register_14_q),
    .in10(register_15_q), .in11(register_16_q), .in12(register_17_q), .in13(register_18_q),
    .in14(register_19_q), .in15(register_20_q), .out(multiplexer_33_out), .sel(Rj));
  Multiplexer #(.select(4), .width(16)) multiplexer_34 (
    .in0(register_5_q), .in1(register_6_q), .in2(register_7_q), .in3(register_8_q), .in4(register_9_q),
    .in5(register_10_q), .in6(register_11_q), .in7(register_12_q), .in8(register_13_q), .in9(register_14_q),
    .in10(register_15_q), .in11(register_16_q), .in12(register_17_q), .in13(register_18_q),
    .in14(register_19_q), .in15(register_20_q), .out(Rdisp), .sel(dispReg));
  Multiplexer #(.width(16)) multiplexer_35 (.in0({16{1'b0}}), .in1(multiplexer_30_out), .out(dataRd), .sel(validRdRe));
  assign xor_2_out = Rj ^ Rd;  // XOR_Gate xor_2, 4 bits wide
  Multiplexer #(.width(16)) multiplexer_36 (.in0(regRs), .in1({{12{1'b0}}, Rs}), .out(dataRs), .sel(iFlag));
  Multiplexer #(.width(16)) multiplexer_37 (
    .in0(multiplexer_33_out), .in1(data), .out(multiplexer_37_out), .sel(and_76_out));
  nor nor_1 (nor_1_out, xor_2_out[0], xor_2_out[1], xor_2_out[2], xor_2_out[3]);
  and and_76 (and_76_out, nor_1_out, we, jmp);
  D_Flip_Flop #(.trigger("falling")) d_ff_2 (
    .D(memOp), .clk(clk), .Qn(d_ff_2_qn), .reset(or_28_out));  // open: Q, preset
  or or_28 (or_28_out, rst, d_ff_3_qn);
  and and_77 (and_77_out, prreg, iFlag);
  or or_29 (or_29_out, and_77_out, expr);
  and and_78 (and_78_out, prreg, iFlag);
  or or_30 (or_30_out, and_78_out, expr);
  and and_79 (and_79_out, prmem, iFlag);
  or or_31 (or_31_out, and_79_out, expr);
  and and_80 (and_80_out, prmem, iFlag);
  or or_32 (or_32_out, and_80_out, expr);
  and and_81 (and_81_out, prprg, iFlag);
  or or_33 (or_33_out, and_81_out, expr);
  and and_82 (and_82_out, prprg, iFlag);
  or or_34 (or_34_out, and_82_out, expr);
  logisim16A_S logisim16A_S_1 (.a(dataRd), .b(dataRs), .OP(sub), .s(logisim16A_S_1_s), .overflow(adderOvfl));
  Multiplexer multiplexer_38 (.in0(immJmp[8]), .in1(1'b0), .out(multiplexer_38_out[6]), .sel(jmpAbs));
  and and_83 (memFrz, memOp, d_ff_2_qn);
  D_Flip_Flop d_ff_3 (.D(memFrz), .clk(clk), .Qn(d_ff_3_qn), .reset(rst));  // open: Q, preset
  Multiplexer #(.width(4)) multiplexer_39 (.in0(Rd), .in1(4'b0000), .out(multiplexer_39_out), .sel(expr));
  freezeReg4 freezeReg4_1 (
    .freeze(memFrz), .D(multiplexer_39_out), .WE(or_29_out), .clk(clk), .R(rst), .Q(prRegReMask));
  Multiplexer #(.width(4)) multiplexer_40 (.in0(Rs), .in1(4'b0000), .out(multiplexer_40_out), .sel(expr));
  freezeReg4 freezeReg4_3 (
    .freeze(memFrz), .D(multiplexer_40_out), .WE(or_30_out), .clk(clk), .R(rst), .Q(prRegReValue));
  Multiplexer #(.width(16)) multiplexer_41 (.in0(dataRd), .in1({16{1'b0}}), .out(multiplexer_41_out), .sel(expr));
  freezeReg16 freezeReg16_10 (
    .freeze(memFrz), .D(multiplexer_41_out), .WE(or_31_out), .clk(clk), .R(rst), .Q(prMemReMask));
  Multiplexer #(.width(16)) multiplexer_42 (.in0(regRs), .in1({16{1'b0}}), .out(multiplexer_42_out), .sel(expr));
  freezeReg16 freezeReg16_12 (
    .freeze(memFrz), .D(multiplexer_42_out), .WE(or_32_out), .clk(clk), .R(rst), .Q(prMemReValue));
  Multiplexer #(.width(16)) multiplexer_43 (.in0(dataRd), .in1({16{1'b0}}), .out(multiplexer_43_out), .sel(expr));
  freezeReg16 freezeReg16_14 (
    .freeze(memFrz), .D(multiplexer_43_out), .WE(or_33_out), .clk(clk), .R(rst), .Q(prPrgReMask));
  Multiplexer #(.width(16)) multiplexer_44 (.in0(regRs), .in1({16{1'b0}}), .out(multiplexer_44_out), .sel(expr));
  freezeReg16 freezeReg16_16 (
    .freeze(memFrz), .D(multiplexer_44_out), .WE(or_34_out), .clk(clk), .R(rst), .Q(prPrgReValue));
  or or_35 (or_35_out, usm, usmz);
  Multiplexer #(.width(7)) multiplexer_45 (
    .in0({7{multiplexer_38_out[6]}}), .in1(dataIn[6:0]), .out(multiplexer_45_out), .sel(exJmp));
  Multiplexer #(.width(16)) multiplexer_46 (
    .in0(logisim16A_S_1_s), .in1(ldData), .out(multiplexer_46_out), .sel(or_36_out));
  or or_36 (or_36_out, pop, ld);
  Multiplexer multiplexer_47 (.in0(d_ff_4_q), .in1(mapOut), .out(utilFlag), .sel(or_35_out));
  Multiplexer multiplexer_48 (.in0(utilFlag), .in1(d_ff_4_q), .out(multiplexer_48_out), .sel(memFrz));
  Multiplexer #(.width(16)) multiplexer_49 (
    .in0(multiplexer_37_out), .in1({multiplexer_45_out, immJmp}), .out(multiplexer_49_out), .sel(or_37_out));
  or or_37 (or_37_out, iJmp, call);
  or or_38 (or_38_out, pshStkExec, popStkExec);
  freezeReg freezeReg_1 (.freeze(memFrz), .D(or_38_out), .we(1'b1), .clk(clk), .R(rst), .Q(frozen));
  D_Flip_Flop d_ff_4 (.D(multiplexer_48_out), .clk(clk), .Q(d_ff_4_q), .reset(rst));  // open: Qn, preset
  and and_84 (and_84_out, or_38_out, not_3_out);
  not not_3 (not_3_out, frozen);
  or or_39 (or_39_out, prhdl, expr);
  Multiplexer #(.width(8)) multiplexer_50 (.in0({8{1'b0}}), .in1(dataIn[7:0]), .out(multiplexer_50_out), .sel(exJmp));
  Multiplexer #(.width(16)) multiplexer_51 (.in0(dataRj), .in1({16{1'b0}}), .out(multiplexer_51_out), .sel(expr));
  freezeReg16 freezeReg16_5 (.freeze(memFrz), .D(multiplexer_51_out), .WE(or_39_out), .clk(clk), .R(rst), .Q(prHdlLoc));
  and and_85 (and_85_out, prreg, ~iFlag);  // AND_Gate
  or or_40 (or_40_out, and_85_out, expr);
  and and_86 (and_86_out, prreg, ~iFlag);  // AND_Gate
  or or_41 (or_41_out, and_86_out, expr);
  and and_87 (and_87_out, prmem, ~iFlag);  // AND_Gate
  or or_42 (or_42_out, and_87_out, expr);
  and and_88 (and_88_out, prmem, ~iFlag);  // AND_Gate
  or or_43 (or_43_out, and_88_out, expr);
  and and_89 (and_89_out, prprg, ~iFlag);  // AND_Gate
  or or_44 (or_44_out, and_89_out, expr);
  and and_90 (and_90_out, prprg, ~iFlag);  // AND_Gate
  or or_45 (or_45_out, and_90_out, expr);
  Multiplexer #(.width(16)) multiplexer_52 (.in0(multiplexer_46_out), .in1(dataRs), .out(multiplexer_52_out), .sel(mv));
  Multiplexer #(.width(16)) multiplexer_53 (
    .in0(multiplexer_37_out), .in1({multiplexer_50_out, altImmJmp}), .out(multiplexer_53_out), .sel(altiJmp));
  or or_46 (freeze, and_84_out, memFrz);
  Multiplexer #(.width(4)) multiplexer_54 (.in0(Rd), .in1(4'b0000), .out(multiplexer_54_out), .sel(expr));
  freezeReg4 freezeReg4_2 (
    .freeze(memFrz), .D(multiplexer_54_out), .WE(or_40_out), .clk(clk), .R(rst), .Q(prRegWrMask));
  Multiplexer #(.width(4)) multiplexer_55 (.in0(Rs), .in1(4'b0000), .out(multiplexer_55_out), .sel(expr));
  freezeReg4 freezeReg4_4 (
    .freeze(memFrz), .D(multiplexer_55_out), .WE(or_41_out), .clk(clk), .R(rst), .Q(prRegWrValue));
  Multiplexer #(.width(16)) multiplexer_56 (.in0(dataRd), .in1({16{1'b0}}), .out(multiplexer_56_out), .sel(expr));
  freezeReg16 freezeReg16_11 (
    .freeze(memFrz), .D(multiplexer_56_out), .WE(or_42_out), .clk(clk), .R(rst), .Q(prMemWrMask));
  Multiplexer #(.width(16)) multiplexer_57 (.in0(regRs), .in1({16{1'b0}}), .out(multiplexer_57_out), .sel(expr));
  freezeReg16 freezeReg16_13 (
    .freeze(memFrz), .D(multiplexer_57_out), .WE(or_43_out), .clk(clk), .R(rst), .Q(prMemWrValue));
  Multiplexer #(.width(16)) multiplexer_58 (.in0(dataRd), .in1({16{1'b0}}), .out(multiplexer_58_out), .sel(expr));
  freezeReg16 freezeReg16_15 (
    .freeze(memFrz), .D(multiplexer_58_out), .WE(or_44_out), .clk(clk), .R(rst), .Q(prPrgWrMask));
  Multiplexer #(.width(16)) multiplexer_59 (.in0(regRs), .in1({16{1'b0}}), .out(multiplexer_59_out), .sel(expr));
  freezeReg16 freezeReg16_17 (
    .freeze(memFrz), .D(multiplexer_59_out), .WE(or_45_out), .clk(clk), .R(rst), .Q(prPrgWrValue));
  bitShift bitShift_1 (
    .rot(bsRot), .left(bsl), .data(dataRd), .amt(dataRs[3:0]), .shifted(bitShift_1_shifted), .oob(bsOob));
  Multiplexer #(.width(16)) multiplexer_60 (
    .in0(multiplexer_49_out), .in1(multiplexer_53_out), .out(multiplexer_60_out), .sel(altJmp));
  Multiplexer #(.width(16)) multiplexer_61 (
    .in0(multiplexer_67_out), .in1(sarRetVal), .out(multiplexer_61_out), .sel(par));
  D_Flip_Flop d_ff_5 (.D(freeze), .clk(clk), .Q(stalled), .reset(rst));  // open: Qn, preset
  Multiplexer #(.width(16)) multiplexer_62 (
    .in0(multiplexer_52_out), .in1(bitShift_1_shifted), .out(multiplexer_62_out), .sel(bs));
  Multiplexer #(.width(16)) multiplexer_63 (
    .in0(multiplexer_60_out), .in1(retVal), .out(multiplexer_63_out), .sel(popStk));
  Multiplexer #(.width(16)) multiplexer_64 (.in0(multiplexer_61_out), .in1(enprRetVal), .out(dataRj), .sel(expr));
  and and_91 (and_91_out, frozen, popStkExec);
  or or_47 (or_47_out, enprExec, parExec);
  Multiplexer #(.width(16)) multiplexer_65 (
    .in0(multiplexer_62_out), .in1(and_92_out), .out(multiplexer_65_out), .sel(bAnd));
  assign and_92_out = dataRd & dataRs;  // AND_Gate and_92, 16 bits wide
  Multiplexer #(.width(16)) multiplexer_66 (
    .in0(multiplexer_71_out), .in1(xor_3_out), .out(multiplexer_66_out), .sel(bXor));
  assign xor_3_out = dataRd ^ dataRs;  // XOR_Gate xor_3, 16 bits wide
  and and_93 (and_93_out, or_47_out, frozen);
  or or_48 (or_48_out, and_93_out, expr, sar);
  or or_49 (or_49_out[0], dataRs[15], dataRs[14], dataRs[13], dataRs[12], dataRs[11], dataRs[10], dataRs[9], dataRs[8], dataRs[7], dataRs[6], dataRs[5], dataRs[4], dataRs[3], dataRs[2], dataRs[1], dataRs[0]);
  Multiplexer #(.width(16)) multiplexer_67 (
    .in0(multiplexer_63_out), .in1(prHdlLoc), .out(multiplexer_67_out), .sel(sar));
  Multiplexer #(.width(16)) multiplexer_68 (.in0(PC), .in1(ldData), .out(multiplexer_68_out), .sel(and_91_out));
  Multiplexer #(.width(16)) multiplexer_69 (
    .in0(multiplexer_68_out), .in1(retVal), .out(multiplexer_69_out), .sel(memFrz));
  or or_50 (or_50_out, and_91_out, pshStkExec);
  freezeReg freezeReg_3 (.freeze(memFrz), .D(and_93_out), .we(or_48_out), .clk(clk), .R(rst), .Q(\protected ));
  assign or_51_out = dataRd | dataRs;  // OR_Gate or_51, 16 bits wide
  Multiplexer #(.width(16)) multiplexer_70 (
    .in0(multiplexer_66_out), .in1({{15{1'b0}}, or_49_out[0]}), .out(multiplexer_70_out), .sel(any));
  Register #(.width(16)) register_21 (.D(multiplexer_69_out), .en(or_50_out), .clk(clk), .Q(retVal), .clr(rst));
  Multiplexer #(.width(16)) multiplexer_71 (
    .in0(multiplexer_65_out), .in1(or_51_out), .out(multiplexer_71_out), .sel(bOr));
  and and_94 (and_94_out, mulOvfl, mul);
  and and_95 (and_95_out, adderOvfl, useAdder);
  and and_96 (and_96_out, bsOob, bsl, bs);
  or or_52 (or_52_out, rst, rstkey);
  // Keyboard keyboard_1: pin names not known; wires that end beside it: CLK_50, clk, or_52_out, PS2_CLK, ldkeyp, PS2_DAT, ldkeyr, rawKey, printKey
  Multiplexer multiplexer_72 (.in0(register_22_q), .in1(or_53_out), .out(ovfl), .sel(or_54_out));
  or or_53 (or_53_out, and_94_out, and_95_out, and_96_out);
  or or_54 (or_54_out, bs, mul, useAdder);
  and and_97 (and_97_out, frozen, pshStkExec);
  Multiplexer #(.width(16)) multiplexer_73 (
    .in0(multiplexer_70_out), .in1({{15{1'b0}}, mapOut}), .out(multiplexer_73_out), .sel(or_55_out));
  or or_55 (or_55_out, lfm, lfmz);
  Register #(.width(1)) register_22 (.D(multiplexer_74_out), .en(or_54_out), .clk(clk), .Q(register_22_q), .clr(rst));
  Multiplexer multiplexer_74 (.in0(or_53_out), .in1(register_22_q), .out(multiplexer_74_out), .sel(memFrz));
  and and_98 (and_98_out, ~frozen, popStkExec);  // AND_Gate
  LED u_ovfl (.in(register_22_q));
  Multiplexer #(.width(16)) multiplexer_75 (.in0(16'h1), .in1({16{1'b1}}), .out(multiplexer_75_out), .sel(or_56_out));
  or or_56 (or_56_out, pop, popStkExec);
  and and_99 (and_99_out, popStkExec, ~frozen);  // AND_Gate
  Multiplexer #(.width(16)) multiplexer_76 (
    .in0(earlyLitStkPtr), .in1(ldData), .out(multiplexer_76_out), .sel(and_98_out));
  or or_57 (or_57_out, and_98_out, and_97_out);
  Multiplexer #(.width(16)) multiplexer_77 (
    .in0(earlyLitStkPtr), .in1(enprFramePtr), .out(multiplexer_77_out), .sel(parExec));
  or or_58 (or_58_out, parExec, enprExec, sarExec);
  and and_100 (and_100_out, or_58_out, frozen);
  and and_101 (and_101_out, sarExec, frozen);
  and and_102 (and_102_out, enprExec, frozen);
  Multiplexer #(.width(16)) multiplexer_78 (.in0(framePtr), .in1(enprFrmPtr), .out(multiplexer_78_out), .sel(exprExec));
  Register #(.width(16)) register_23 (.D(multiplexer_79_out), .en(or_57_out), .clk(clk), .Q(framePtr), .clr(rst));
  Multiplexer #(.width(16)) multiplexer_79 (
    .in0(multiplexer_76_out), .in1(framePtr), .out(multiplexer_79_out), .sel(memFrz));
  freezeReg16 freezeReg16_4 (
    .freeze(memFrz), .D(multiplexer_77_out), .WE(and_100_out), .clk(clk), .R(rst), .Q(freezeReg16_4_q));
  freezeReg16 freezeReg16_8 (.freeze(memFrz), .D(earlyLitStkPtr), .WE(and_102_out), .clk(clk), .R(rst), .Q(enprFrmPtr));
  Multiplexer #(.width(16)) multiplexer_80 (
    .in0(multiplexer_78_out), .in1(sarFrmPtr), .out(multiplexer_80_out), .sel(parExec));
  freezeReg16 freezeReg16_6 (.freeze(memFrz), .D(earlyLitStkPtr), .WE(and_101_out), .clk(clk), .R(rst), .Q(sarFrmPtr));
  Multiplexer multiplexer_81 (.in0(register_24_q), .in1(and_103_out), .out(unfl), .sel(bs));
  Multiplexer multiplexer_82 (.in0(and_103_out), .in1(register_24_q), .out(multiplexer_82_out), .sel(memFrz));
  and and_103 (and_103_out, bsOob, ~bsl, bs);  // AND_Gate
  Multiplexer #(.width(16)) multiplexer_83 (
    .in0(litStkPtr), .in1(multiplexer_80_out), .out(multiplexer_83_out), .sel(and_99_out));
  assign xor_4_out = freezeReg16_4_q ^ framePtr;  // XOR_Gate xor_4, 16 bits wide
  highestSetBit highestSetBit_1 (.data(dataRd), .hsb(highestSetBit_1_hsb));
  Register #(.width(1)) register_24 (.D(multiplexer_82_out), .en(bs), .clk(clk), .Q(register_24_q), .clr(rst));
  Adder #(.width(16)) adder_2 (
    .a(multiplexer_83_out), .b(multiplexer_75_out), .out(earlyLitStkPtr));  // open: cin, cout
  Register #(.width(16)) register_25 (.D(multiplexer_84_out), .en(or_59_out), .clk(clk), .Q(litStkPtr), .clr(rst));
  Multiplexer #(.width(16)) multiplexer_84 (
    .in0(earlyLitStkPtr), .in1(litStkPtr), .out(multiplexer_84_out), .sel(memFrz));
  or or_59 (or_59_out, pop, popStkExec, pshStkExec, push);
  Multiplexer #(.width(16)) multiplexer_85 (
    .in0(multiplexer_73_out), .in1(highestSetBit_1_hsb), .out(multiplexer_85_out), .sel(hsb));
  or or_60 (stkPopAllowed, xor_4_out[0], xor_4_out[1], xor_4_out[2], xor_4_out[3], xor_4_out[4], xor_4_out[5], xor_4_out[6], xor_4_out[7], xor_4_out[8], xor_4_out[9], xor_4_out[10], xor_4_out[11], xor_4_out[12], xor_4_out[13], xor_4_out[14], xor_4_out[15]);
  // RGB_Video rgb_video_1: pin names not known; wires that end beside it: CLK_50, clk, stchr, dataRs[10:0], dataRd[7:0], VGA_R, VGA_G, VGA_B, VGA_CLK, VGA_SYNC_N, VGA_BLANK_N, VGA_HS, VGA_VS
  assign stackPtr = ~litStkPtr;  // NOT_Gate not_4, 16 bits wide
  and and_104 (and_104_out, sarExec, frozen);
  and and_105 (and_105_out, enprExec, frozen);
  freezeReg16 freezeReg16_9 (.freeze(memFrz), .D(PC), .WE(and_105_out), .clk(clk), .R(rst), .Q(enprRetVal));
  assign earlyStackPtr = ~earlyLitStkPtr;  // NOT_Gate not_5, 16 bits wide
  freezeReg16 freezeReg16_7 (.freeze(memFrz), .D(PC), .WE(and_104_out), .clk(clk), .R(rst), .Q(sarRetVal));
  mul16 mul16_1 (.A(dataRd), .B(dataRs), .s(isSignedMul), .AB(mul16_1_ab), .O(mulOvfl));
  Multiplexer #(.width(16)) multiplexer_86 (
    .in0(multiplexer_85_out), .in1(mul16_1_ab), .out(multiplexer_86_out), .sel(mul));
  Multiplexer #(.width(16)) multiplexer_87 (
    .in0(multiplexer_86_out), .in1({16{1'b0}}), .out(multiplexer_87_out), .sel(and_106_out));
  and and_106 (and_106_out, ~pop, popIR);  // AND_Gate
  Multiplexer #(.width(16)) multiplexer_88 (
    .in0(multiplexer_87_out), .in1({{8{1'b0}}, keyBuffer}), .out(data), .sel(ldkey));

  // Notes on the sheet:
  //   Inputs
  //   Cycle Counter
  //   Segfault Detection
  //   Data Memory
  //   Masked Operations
  //   Instruction Flags
  //   Jump Logic
  //   REMOVE FOR FPGA
  //   Program Loader
  //   REMOVE FOR FPGA
  //   Flag Map
  //   IR Handling
  //   Hex Display
  //   Data Handling
  //   Freeze Pipeline
  //   Util Register
  //   Prot Bitmaps and Values
  //   Prot Handle Loc
  //   Current Return Address
  //   Protected Flag
  //   Keyboard
  //   Overflow/Underflow
  //   Protected Stack Bottom
  //   Frame Pointer
  //   Stack Pointer
  //   SAR Frame Header
  //   ENPR Frame Header
  //   Video
endmodule

module programCounter (
  input  [15:0] jmpVal,
  input  jmp,
  input  jmpAbs,
  input  clk,
  input  rst,
  input  freeze,
  output [15:0] pc
);

  wire and_1_out, and_2_out;
  wire [15:0] adder_1_out, freezeReg16_1_q, freezeReg16_3_q, multiplexer_1_out, multiplexer_2_out,
       multiplexer_3_out;

  Multiplexer #(.width(16)) multiplexer_1 (.in0(16'h1), .in1(jmpVal), .out(multiplexer_1_out), .sel(and_1_out));
  and and_1 (and_1_out, jmp, ~jmpAbs);  // AND_Gate
  Multiplexer #(.width(16)) multiplexer_2 (.in0(pc), .in1(freezeReg16_3_q), .out(multiplexer_2_out), .sel(and_1_out));
  Adder #(.width(16)) adder_1 (.a(multiplexer_2_out), .b(multiplexer_1_out), .out(adder_1_out));  // open: cin, cout
  and and_2 (and_2_out, jmp, jmpAbs);
  Multiplexer #(.width(16)) multiplexer_3 (.in0(adder_1_out), .in1(jmpVal), .out(multiplexer_3_out), .sel(and_2_out));
  freezeReg16 freezeReg16_2 (.freeze(freeze), .D(multiplexer_3_out), .WE(1'b1), .clk(clk), .R(rst), .Q(pc));
  freezeReg16 freezeReg16_1 (.freeze(freeze), .D(pc), .WE(1'b1), .clk(clk), .R(rst), .Q(freezeReg16_1_q));
  freezeReg16 freezeReg16_3 (.freeze(freeze), .D(freezeReg16_1_q), .WE(1'b1), .clk(clk), .R(rst), .Q(freezeReg16_3_q));
endmodule

module cycleCounter (
  input  clk,
  input  rst,
  input  freeze,
  output [15:0] cycles
);

  wire [15:0] adder_1_out;

  Adder #(.width(16)) adder_1 (.a(cycles), .b(16'h1), .out(adder_1_out));  // open: cin, cout
  freezeReg16 freezeReg16_1 (.freeze(freeze), .D(adder_1_out), .WE(1'b1), .clk(clk), .R(rst), .Q(cycles));
endmodule

module jumpDecoder (
  input  [15:0] IR,
  output [2:0] flags,
  output absolute,
  output jmp,
  output i,
  output [3:0] Rj,
  output [8:0] immediate,
  output alti,
  output [7:0] altImm,
  output call,
  output ret,
  output prhdl,
  output altJmp,
  output enpr,
  output expr,
  output sar,
  output par
);

  and and_1 (call, ~IR[0], ~IR[1], IR[2], ~IR[3], IR[4], ~IR[5], ~IR[6]);  // AND_Gate
  and and_2 (ret, IR[0], ~IR[1], IR[2], ~IR[3], IR[4], ~IR[5], ~IR[6]);  // AND_Gate
  and and_3 (prhdl, ~IR[0], ~IR[1], IR[2], ~IR[3], ~IR[4], IR[5], ~IR[6]);  // AND_Gate
  and and_4 (enpr, IR[0], ~IR[1], IR[2], ~IR[3], ~IR[4], IR[5], ~IR[6]);  // AND_Gate
  and and_5 (expr, ~IR[0], IR[1], IR[2], ~IR[3], ~IR[4], IR[5], ~IR[6]);  // AND_Gate
  and and_6 (sar, IR[0], IR[1], IR[2], ~IR[3], ~IR[4], IR[5], ~IR[6]);  // AND_Gate
  and and_7 (par, ~IR[0], ~IR[1], ~IR[2], IR[3], ~IR[4], IR[5], ~IR[6]);  // AND_Gate
  and and_8 (jmp, ~IR[5], IR[6]);  // AND_Gate
  or or_1 (altJmp, prhdl, enpr);

  assign absolute = IR[4];
  assign alti = IR[7];
  assign altImm = IR[15:8];
  assign flags = IR[2:0];
  assign i = IR[3];
  assign immediate = IR[15:7];
  assign Rj = IR[10:7];
endmodule

module IRDecoder (
  input  clk,
  input  rst,
  input  freeze,
  input  [15:0] IR,
  output [8:0] dataIn,
  output [3:0] Rs,
  output [3:0] Rd,
  output i,
  output nop,
  output add,
  output sub,
  output ld,
  output mv,
  output st,
  output halt,
  output bs,
  output bsLeft,
  output bsRot,
  output bAnd,
  output bOr,
  output bXor,
  output any,
  output lfm,
  output lfmz,
  output usm,
  output usmz,
  output hsb,
  output exJmp,
  output call,
  output ret,
  output isSignedMul,
  output mul,
  output push,
  output pop,
  output prreg,
  output prmem,
  output prprg,
  output enpr,
  output expr,
  output sar,
  output par,
  output ldkeyr,
  output stchr,
  output ldkeyp,
  output rstkey
);

  wire and_1_out, and_2_out, and_3_out, and_4_out, and_5_out, and_6_out, and_7_out, and_8_out, and_9_out,
       and_10_out, and_11_out, and_12_out, and_13_out, and_14_out, and_15_out, and_16_out, and_17_out,
       and_18_out, and_19_out, and_20_out, and_21_out, and_22_out, and_23_out, and_24_out, and_25_out,
       and_26_out, and_27_out, and_28_out, and_29_out, and_30_out, and_31_out, and_32_out, and_33_out,
       and_34_out, freezeReg_10_q, freezeReg_24_q;

  freezeReg9 freezeReg9_1 (.freeze(freeze), .D(IR[15:7]), .WE(1'b1), .clk(clk), .R(rst), .Q(dataIn));
  freezeReg4 freezeReg4_1 (.freeze(freeze), .D(IR[11:8]), .WE(1'b1), .clk(clk), .R(rst), .Q(Rs));
  freezeReg4 freezeReg4_2 (.freeze(freeze), .D(IR[15:12]), .WE(1'b1), .clk(clk), .R(rst), .Q(Rd));
  freezeReg freezeReg_1 (.freeze(freeze), .D(IR[7]), .we(1'b1), .clk(clk), .R(rst), .Q(i));
  and and_1 (and_1_out, ~IR[0], ~IR[1], ~IR[2], ~IR[3], ~IR[4], ~IR[5], ~IR[6]);  // AND_Gate
  and and_2 (and_2_out, IR[0], ~IR[1], ~IR[2], ~IR[3], ~IR[4], ~IR[5], ~IR[6]);  // AND_Gate
  and and_3 (and_3_out, ~IR[0], IR[1], ~IR[2], ~IR[3], ~IR[4], ~IR[5], ~IR[6]);  // AND_Gate
  and and_4 (and_4_out, IR[0], IR[1], ~IR[2], ~IR[3], ~IR[4], ~IR[5], ~IR[6]);  // AND_Gate
  and and_5 (and_5_out, ~IR[0], ~IR[1], IR[2], ~IR[3], ~IR[4], ~IR[5], ~IR[6]);  // AND_Gate
  and and_6 (and_6_out, IR[0], ~IR[1], IR[2], ~IR[3], ~IR[4], ~IR[5], ~IR[6]);  // AND_Gate
  and and_7 (and_7_out, IR[0], IR[1], IR[2], IR[3], IR[4], IR[5], IR[6]);
  and and_8 (and_8_out, IR[2], IR[3], ~IR[4], ~IR[5], ~IR[6]);  // AND_Gate
  and and_9 (and_9_out, ~IR[0], ~IR[1], ~IR[2], ~IR[3], IR[4], ~IR[5], ~IR[6]);  // AND_Gate
  and and_10 (and_10_out, IR[0], ~IR[1], ~IR[2], ~IR[3], IR[4], ~IR[5], ~IR[6]);  // AND_Gate
  and and_11 (and_11_out, ~IR[0], IR[1], ~IR[2], ~IR[3], IR[4], ~IR[5], ~IR[6]);  // AND_Gate
  and and_12 (and_12_out, IR[0], IR[1], ~IR[2], ~IR[3], IR[4], ~IR[5], ~IR[6]);  // AND_Gate
  and and_13 (and_13_out, ~IR[0], IR[1], IR[2], ~IR[3], IR[4], ~IR[5], ~IR[6]);  // AND_Gate
  and and_14 (and_14_out, ~IR[0], IR[1], ~IR[2], IR[3], IR[4], ~IR[5], ~IR[6]);  // AND_Gate
  and and_15 (and_15_out, IR[0], IR[1], IR[2], ~IR[3], IR[4], ~IR[5], ~IR[6]);  // AND_Gate
  and and_16 (and_16_out, ~IR[0], ~IR[1], ~IR[2], IR[3], IR[4], ~IR[5], ~IR[6]);  // AND_Gate
  and and_17 (and_17_out, IR[0], IR[1], ~IR[2], IR[3], IR[4], ~IR[5], ~IR[6]);  // AND_Gate
  and and_18 (and_18_out, ~IR[0], IR[1], IR[2], IR[3], IR[4], ~IR[5], ~IR[6]);  // AND_Gate
  and and_19 (and_19_out, ~IR[0], ~IR[1], IR[2], ~IR[3], IR[4], ~IR[5], ~IR[6]);  // AND_Gate
  and and_20 (and_20_out, IR[0], ~IR[1], IR[2], ~IR[3], IR[4], ~IR[5], ~IR[6]);  // AND_Gate
  and and_21 (and_21_out, IR[1], IR[2], ~IR[3], ~IR[4], ~IR[5], ~IR[6]);  // AND_Gate
  and and_22 (and_22_out, ~IR[0], ~IR[1], ~IR[2], IR[3], ~IR[4], ~IR[5], ~IR[6]);  // AND_Gate
  and and_23 (and_23_out, IR[0], ~IR[1], ~IR[2], IR[3], ~IR[4], ~IR[5], ~IR[6]);  // AND_Gate
  and and_24 (and_24_out, ~IR[0], ~IR[1], ~IR[2], ~IR[3], ~IR[4], IR[5], ~IR[6]);  // AND_Gate
  and and_25 (and_25_out, IR[0], ~IR[1], ~IR[2], ~IR[3], ~IR[4], IR[5], ~IR[6]);  // AND_Gate
  and and_26 (and_26_out, ~IR[0], IR[1], ~IR[2], ~IR[3], ~IR[4], IR[5], ~IR[6]);  // AND_Gate
  and and_27 (and_27_out, IR[0], ~IR[1], IR[2], ~IR[3], ~IR[4], IR[5], ~IR[6]);  // AND_Gate
  and and_28 (and_28_out, ~IR[0], IR[1], IR[2], ~IR[3], ~IR[4], IR[5], ~IR[6]);  // AND_Gate
  and and_29 (and_29_out, IR[0], IR[1], IR[2], ~IR[3], ~IR[4], IR[5], ~IR[6]);  // AND_Gate
  and and_30 (and_30_out, ~IR[0], ~IR[1], ~IR[2], IR[3], ~IR[4], IR[5], ~IR[6]);  // AND_Gate
  and and_31 (and_31_out, IR[0], IR[1], ~IR[2], ~IR[3], ~IR[4], ~IR[5], ~IR[6]);  // AND_Gate
  and and_32 (and_32_out, IR[0], IR[1], ~IR[2], IR[3], ~IR[4], ~IR[5], ~IR[6]);  // AND_Gate
  and and_33 (and_33_out, IR[0], IR[1], ~IR[2], ~IR[3], ~IR[4], ~IR[5], IR[6]);  // AND_Gate
  and and_34 (and_34_out, IR[0], IR[1], ~IR[2], ~IR[3], ~IR[4], IR[5], ~IR[6]);  // AND_Gate
  freezeReg freezeReg_2 (.freeze(freeze), .D(and_1_out), .we(1'b1), .clk(clk), .R(rst), .Q(nop));
  freezeReg freezeReg_3 (.freeze(freeze), .D(and_2_out), .we(1'b1), .clk(clk), .R(rst), .Q(add));
  freezeReg freezeReg_4 (.freeze(freeze), .D(and_3_out), .we(1'b1), .clk(clk), .R(rst), .Q(sub));
  freezeReg freezeReg_5 (.freeze(freeze), .D(and_4_out), .we(1'b1), .clk(clk), .R(rst), .Q(ld));
  freezeReg freezeReg_6 (.freeze(freeze), .D(and_5_out), .we(1'b1), .clk(clk), .R(rst), .Q(mv));
  freezeReg freezeReg_7 (.freeze(freeze), .D(and_6_out), .we(1'b1), .clk(clk), .R(rst), .Q(st));
  freezeReg freezeReg_8 (.freeze(freeze), .D(and_7_out), .we(1'b1), .clk(clk), .R(rst), .Q(halt));
  freezeReg freezeReg_9 (.freeze(freeze), .D(and_8_out), .we(1'b1), .clk(clk), .R(rst), .Q(bs));
  freezeReg freezeReg_10 (.freeze(freeze), .D(IR[0]), .we(1'b1), .clk(clk), .R(rst), .Q(freezeReg_10_q));
  freezeReg freezeReg_11 (.freeze(freeze), .D(IR[1]), .we(1'b1), .clk(clk), .R(rst), .Q(bsRot));
  freezeReg freezeReg_12 (.freeze(freeze), .D(and_9_out), .we(1'b1), .clk(clk), .R(rst), .Q(bAnd));
  freezeReg freezeReg_13 (.freeze(freeze), .D(and_10_out), .we(1'b1), .clk(clk), .R(rst), .Q(bOr));
  freezeReg freezeReg_14 (.freeze(freeze), .D(and_11_out), .we(1'b1), .clk(clk), .R(rst), .Q(bXor));
  freezeReg freezeReg_15 (.freeze(freeze), .D(and_12_out), .we(1'b1), .clk(clk), .R(rst), .Q(any));
  freezeReg freezeReg_16 (.freeze(freeze), .D(and_13_out), .we(1'b1), .clk(clk), .R(rst), .Q(lfm));
  freezeReg freezeReg_17 (.freeze(freeze), .D(and_14_out), .we(1'b1), .clk(clk), .R(rst), .Q(lfmz));
  freezeReg freezeReg_18 (.freeze(freeze), .D(and_15_out), .we(1'b1), .clk(clk), .R(rst), .Q(usm));
  freezeReg freezeReg_19 (.freeze(freeze), .D(and_16_out), .we(1'b1), .clk(clk), .R(rst), .Q(usmz));
  freezeReg freezeReg_20 (.freeze(freeze), .D(and_17_out), .we(1'b1), .clk(clk), .R(rst), .Q(hsb));
  freezeReg freezeReg_21 (.freeze(freeze), .D(and_18_out), .we(1'b1), .clk(clk), .R(rst), .Q(exJmp));
  freezeReg freezeReg_22 (.freeze(freeze), .D(and_19_out), .we(1'b1), .clk(clk), .R(rst), .Q(call));
  freezeReg freezeReg_23 (.freeze(freeze), .D(and_20_out), .we(1'b1), .clk(clk), .R(rst), .Q(ret));
  freezeReg freezeReg_24 (.freeze(freeze), .D(IR[0]), .we(1'b1), .clk(clk), .R(rst), .Q(freezeReg_24_q));
  freezeReg freezeReg_25 (.freeze(freeze), .D(and_21_out), .we(1'b1), .clk(clk), .R(rst), .Q(mul));
  freezeReg freezeReg_26 (.freeze(freeze), .D(and_22_out), .we(1'b1), .clk(clk), .R(rst), .Q(push));
  freezeReg freezeReg_27 (.freeze(freeze), .D(and_23_out), .we(1'b1), .clk(clk), .R(rst), .Q(pop));
  freezeReg freezeReg_28 (.freeze(freeze), .D(and_24_out), .we(1'b1), .clk(clk), .R(rst), .Q(prreg));
  freezeReg freezeReg_29 (.freeze(freeze), .D(and_25_out), .we(1'b1), .clk(clk), .R(rst), .Q(prmem));
  freezeReg freezeReg_30 (.freeze(freeze), .D(and_26_out), .we(1'b1), .clk(clk), .R(rst), .Q(prprg));
  freezeReg freezeReg_31 (.freeze(freeze), .D(and_27_out), .we(1'b1), .clk(clk), .R(rst), .Q(enpr));
  freezeReg freezeReg_32 (.freeze(freeze), .D(and_28_out), .we(1'b1), .clk(clk), .R(rst), .Q(expr));
  freezeReg freezeReg_33 (.freeze(freeze), .D(and_29_out), .we(1'b1), .clk(clk), .R(rst), .Q(sar));
  freezeReg freezeReg_34 (.freeze(freeze), .D(and_30_out), .we(1'b1), .clk(clk), .R(rst), .Q(par));
  freezeReg freezeReg_35 (.freeze(freeze), .D(and_31_out), .we(1'b1), .clk(clk), .R(rst), .Q(ldkeyr));
  freezeReg freezeReg_36 (.freeze(freeze), .D(and_32_out), .we(1'b1), .clk(clk), .R(rst), .Q(stchr));
  freezeReg freezeReg_37 (.freeze(freeze), .D(and_33_out), .we(1'b1), .clk(clk), .R(rst), .Q(ldkeyp));
  freezeReg freezeReg_38 (.freeze(freeze), .D(and_34_out), .we(1'b1), .clk(clk), .R(rst), .Q(rstkey));
  not not_1 (bsLeft, freezeReg_10_q);
  not not_2 (isSignedMul, freezeReg_24_q);

  // Other names for the same wires on the sheet: frz = freeze
endmodule

module bitShift (
  input  rot,
  input  left,
  input  [15:0] data,
  input  [3:0] amt,
  output [15:0] shifted,
  output oob
);

  wire a, b, c, d, e, f, g, h, i, j, k, l, la, lb, lc, ld, le, lf, lg, lh, li, lj, lk, ll, lm, ln, lo, lp, m,
       multiplexer_5_out, multiplexer_6_out, multiplexer_9_out, multiplexer_11_out, multiplexer_13_out,
       multiplexer_14_out, multiplexer_17_out, multiplexer_19_out, multiplexer_21_out, multiplexer_22_out,
       multiplexer_25_out, multiplexer_27_out, multiplexer_29_out, multiplexer_30_out, multiplexer_33_out, n,
       o, p;
  wire [15:0] multiplexer_2_out, reverse16_1_output_bus_1, reverse16_2_output_bus_1;

  and and_1 (la, a, rot);
  and and_2 (lb, b, rot);
  and and_3 (lc, c, rot);
  and and_4 (ld, d, rot);
  and and_5 (le, e, rot);
  and and_6 (lf, f, rot);
  and and_7 (lg, g, rot);
  and and_8 (lh, h, rot);
  and and_9 (li, i, rot);
  and and_10 (lj, j, rot);
  and and_11 (lk, k, rot);
  and and_12 (ll, l, rot);
  and and_13 (lm, m, rot);
  and and_14 (ln, n, rot);
  and and_15 (lo, o, rot);
  and and_16 (lp, p, rot);
  Multiplexer #(.width(16)) multiplexer_1 (
    .in0(multiplexer_2_out), .in1(reverse16_2_output_bus_1), .out(shifted), .sel(left));
  reverse16 reverse16_2 (.Input_bus_1(multiplexer_2_out), .Output_bus_1(reverse16_2_output_bus_1));
  or or_1 (oob, multiplexer_5_out, multiplexer_6_out, multiplexer_9_out, multiplexer_11_out, multiplexer_13_out, multiplexer_14_out, multiplexer_17_out, multiplexer_19_out, multiplexer_21_out, multiplexer_22_out, multiplexer_25_out, multiplexer_27_out, multiplexer_29_out, multiplexer_30_out, multiplexer_33_out);
  Multiplexer #(.select(4)) multiplexer_2 (
    .in0(a), .in1(b), .in2(c), .in3(d), .in4(e), .in5(f), .in6(g), .in7(h), .in8(i), .in9(j), .in10(k),
    .in11(l), .in12(m), .in13(n), .in14(o), .in15(p), .out(multiplexer_2_out[0]), .sel(amt));
  reverse16 reverse16_1 (.Input_bus_1(data), .Output_bus_1(reverse16_1_output_bus_1));
  Multiplexer #(.width(16)) multiplexer_3 (
    .in0(data), .in1(reverse16_1_output_bus_1), .out({p, o, n, m, l, k, j, i, h, g, f, e, d, c, b, a}),
    .sel(left));
  Multiplexer #(.select(4)) multiplexer_4 (
    .in0(b), .in1(c), .in2(d), .in3(e), .in4(f), .in5(g), .in6(h), .in7(i), .in8(j), .in9(j), .in10(l),
    .in11(m), .in12(n), .in13(o), .in14(p), .in15(la), .out(multiplexer_2_out[1]), .sel(amt));
  Multiplexer #(.select(4)) multiplexer_5 (
    .in0(1'b0), .in1(1'b0), .in2(1'b0), .in3(1'b0), .in4(1'b0), .in5(1'b0), .in6(1'b0), .in7(1'b0),
    .in8(1'b0), .in9(1'b0), .in10(1'b0), .in11(1'b0), .in12(1'b0), .in13(1'b0), .in14(1'b0), .in15(a),
    .out(multiplexer_5_out), .sel(amt));
  Multiplexer #(.select(4)) multiplexer_6 (
    .in0(1'b0), .in1(1'b0), .in2(1'b0), .in3(1'b0), .in4(1'b0), .in5(1'b0), .in6(1'b0), .in7(1'b0),
    .in8(1'b0), .in9(1'b0), .in10(1'b0), .in11(1'b0), .in12(1'b0), .in13(1'b0), .in14(a), .in15(b),
    .out(multiplexer_6_out), .sel(amt));
  Multiplexer #(.select(4)) multiplexer_7 (
    .in0(c), .in1(d), .in2(e), .in3(f), .in4(g), .in5(h), .in6(i), .in7(j), .in8(k), .in9(l), .in10(m),
    .in11(n), .in12(o), .in13(p), .in14(la), .in15(lb), .out(multiplexer_2_out[2]), .sel(amt));
  Multiplexer #(.select(4)) multiplexer_8 (
    .in0(d), .in1(e), .in2(f), .in3(g), .in4(h), .in5(i), .in6(j), .in7(k), .in8(l), .in9(m), .in10(n),
    .in11(o), .in12(p), .in13(la), .in14(lb), .in15(lc), .out(multiplexer_2_out[3]), .sel(amt));
  Multiplexer #(.select(4)) multiplexer_9 (
    .in0(1'b0), .in1(1'b0), .in2(1'b0), .in3(1'b0), .in4(1'b0), .in5(1'b0), .in6(1'b0), .in7(1'b0),
    .in8(1'b0), .in9(1'b0), .in10(1'b0), .in11(1'b0), .in12(1'b0), .in13(a), .in14(b), .in15(c),
    .out(multiplexer_9_out), .sel(amt));
  Multiplexer #(.select(4)) multiplexer_10 (
    .in0(e), .in1(f), .in2(g), .in3(h), .in4(i), .in5(j), .in6(k), .in7(l), .in8(m), .in9(n), .in10(o),
    .in11(p), .in12(la), .in13(lb), .in14(lc), .in15(ld), .out(multiplexer_2_out[4]), .sel(amt));
  Multiplexer #(.select(4)) multiplexer_11 (
    .in0(1'b0), .in1(1'b0), .in2(1'b0), .in3(1'b0), .in4(1'b0), .in5(1'b0), .in6(1'b0), .in7(1'b0),
    .in8(1'b0), .in9(1'b0), .in10(1'b0), .in11(1'b0), .in12(a), .in13(b), .in14(c), .in15(d),
    .out(multiplexer_11_out), .sel(amt));
  Multiplexer #(.select(4)) multiplexer_12 (
    .in0(f), .in1(g), .in2(h), .in3(i), .in4(j), .in5(k), .in6(l), .in7(m), .in8(n), .in9(o), .in10(p),
    .in11(la), .in12(lb), .in13(lc), .in14(ld), .in15(le), .out(multiplexer_2_out[5]), .sel(amt));
  Multiplexer #(.select(4)) multiplexer_13 (
    .in0(1'b0), .in1(1'b0), .in2(1'b0), .in3(1'b0), .in4(1'b0), .in5(1'b0), .in6(1'b0), .in7(1'b0),
    .in8(1'b0), .in9(1'b0), .in10(1'b0), .in11(a), .in12(b), .in13(c), .in14(d), .in15(e),
    .out(multiplexer_13_out), .sel(amt));
  Multiplexer #(.select(4)) multiplexer_14 (
    .in0(1'b0), .in1(1'b0), .in2(1'b0), .in3(1'b0), .in4(1'b0), .in5(1'b0), .in6(1'b0), .in7(1'b0),
    .in8(1'b0), .in9(1'b0), .in10(a), .in11(b), .in12(c), .in13(d), .in14(e), .in15(f),
    .out(multiplexer_14_out), .sel(amt));
  Multiplexer #(.select(4)) multiplexer_15 (
    .in0(g), .in1(h), .in2(i), .in3(j), .in4(k), .in5(l), .in6(m), .in7(n), .in8(o), .in9(p), .in10(la),
    .in11(lb), .in12(lc), .in13(ld), .in14(le), .in15(lf), .out(multiplexer_2_out[6]), .sel(amt));
  Multiplexer #(.select(4)) multiplexer_16 (
    .in0(h), .in1(i), .in2(j), .in3(k), .in4(l), .in5(m), .in6(n), .in7(o), .in8(p), .in9(la), .in10(lb),
    .in11(lc), .in12(ld), .in13(le), .in14(lf), .in15(lg), .out(multiplexer_2_out[7]), .sel(amt));
  Multiplexer #(.select(4)) multiplexer_17 (
    .in0(1'b0), .in1(1'b0), .in2(1'b0), .in3(1'b0), .in4(1'b0), .in5(1'b0), .in6(1'b0), .in7(1'b0),
    .in8(1'b0), .in9(a), .in10(b), .in11(c), .in12(d), .in13(e), .in14(f), .in15(g),
    .out(multiplexer_17_out), .sel(amt));
  Multiplexer #(.select(4)) multiplexer_18 (
    .in0(i), .in1(j), .in2(k), .in3(l), .in4(m), .in5(n), .in6(o), .in7(p), .in8(la), .in9(lb), .in10(lc),
    .in11(ld), .in12(le), .in13(lf), .in14(lg), .in15(lh), .out(multiplexer_2_out[8]), .sel(amt));
  Multiplexer #(.select(4)) multiplexer_19 (
    .in0(1'b0), .in1(1'b0), .in2(1'b0), .in3(1'b0), .in4(1'b0), .in5(1'b0), .in6(1'b0), .in7(1'b0), .in8(a),
    .in9(b), .in10(c), .in11(d), .in12(e), .in13(f), .in14(g), .in15(h), .out(multiplexer_19_out), .sel(amt));
  Multiplexer #(.select(4)) multiplexer_20 (
    .in0(j), .in1(k), .in2(l), .in3(m), .in4(n), .in5(o), .in6(p), .in7(la), .in8(lb), .in9(lc), .in10(ld),
    .in11(le), .in12(lf), .in13(lg), .in14(lh), .in15(li), .out(multiplexer_2_out[9]), .sel(amt));
  Multiplexer #(.select(4)) multiplexer_21 (
    .in0(1'b0), .in1(1'b0), .in2(1'b0), .in3(1'b0), .in4(1'b0), .in5(1'b0), .in6(1'b0), .in7(a), .in8(b),
    .in9(c), .in10(d), .in11(e), .in12(f), .in13(g), .in14(h), .in15(i), .out(multiplexer_21_out), .sel(amt));
  Multiplexer #(.select(4)) multiplexer_22 (
    .in0(1'b0), .in1(1'b0), .in2(1'b0), .in3(1'b0), .in4(1'b0), .in5(1'b0), .in6(a), .in7(b), .in8(c),
    .in9(d), .in10(e), .in11(f), .in12(g), .in13(h), .in14(i), .in15(j), .out(multiplexer_22_out), .sel(amt));
  Multiplexer #(.select(4)) multiplexer_23 (
    .in0(k), .in1(l), .in2(m), .in3(n), .in4(o), .in5(p), .in6(la), .in7(lb), .in8(lc), .in9(ld), .in10(le),
    .in11(lf), .in12(lg), .in13(lh), .in14(li), .in15(lj), .out(multiplexer_2_out[10]), .sel(amt));
  Multiplexer #(.select(4)) multiplexer_24 (
    .in0(l), .in1(m), .in2(n), .in3(o), .in4(p), .in5(la), .in6(lb), .in7(lc), .in8(ld), .in9(le), .in10(lf),
    .in11(lg), .in12(lh), .in13(li), .in14(lj), .in15(lk), .out(multiplexer_2_out[11]), .sel(amt));
  Multiplexer #(.select(4)) multiplexer_25 (
    .in0(1'b0), .in1(1'b0), .in2(1'b0), .in3(1'b0), .in4(1'b0), .in5(a), .in6(b), .in7(c), .in8(d), .in9(e),
    .in10(f), .in11(g), .in12(h), .in13(i), .in14(j), .in15(k), .out(multiplexer_25_out), .sel(amt));
  Multiplexer #(.select(4)) multiplexer_26 (
    .in0(m), .in1(n), .in2(o), .in3(p), .in4(la), .in5(lb), .in6(lc), .in7(ld), .in8(le), .in9(lf),
    .in10(lg), .in11(lh), .in12(li), .in13(lj), .in14(lk), .in15(ll), .out(multiplexer_2_out[12]), .sel(amt));
  Multiplexer #(.select(4)) multiplexer_27 (
    .in0(1'b0), .in1(1'b0), .in2(1'b0), .in3(1'b0), .in4(a), .in5(b), .in6(c), .in7(d), .in8(e), .in9(f),
    .in10(g), .in11(h), .in12(i), .in13(j), .in14(k), .in15(l), .out(multiplexer_27_out), .sel(amt));
  Multiplexer #(.select(4)) multiplexer_28 (
    .in0(n), .in1(o), .in2(p), .in3(la), .in4(lb), .in5(lc), .in6(ld), .in7(le), .in8(lf), .in9(lg),
    .in10(lh), .in11(li), .in12(lj), .in13(lk), .in14(ll), .in15(lm), .out(multiplexer_2_out[13]), .sel(amt));
  Multiplexer #(.select(4)) multiplexer_29 (
    .in0(1'b0), .in1(1'b0), .in2(1'b0), .in3(a), .in4(b), .in5(c), .in6(d), .in7(e), .in8(f), .in9(g),
    .in10(h), .in11(i), .in12(j), .in13(k), .in14(l), .in15(m), .out(multiplexer_29_out), .sel(amt));
  Multiplexer #(.select(4)) multiplexer_30 (
    .in0(1'b0), .in1(1'b0), .in2(a), .in3(b), .in4(c), .in5(d), .in6(e), .in7(f), .in8(g), .in9(h), .in10(i),
    .in11(j), .in12(k), .in13(l), .in14(m), .in15(n), .out(multiplexer_30_out), .sel(amt));
  Multiplexer #(.select(4)) multiplexer_31 (
    .in0(o), .in1(p), .in2(la), .in3(lb), .in4(lc), .in5(ld), .in6(le), .in7(lf), .in8(lg), .in9(lh),
    .in10(li), .in11(lj), .in12(lk), .in13(ll), .in14(lm), .in15(ln), .out(multiplexer_2_out[14]), .sel(amt));
  Multiplexer #(.select(4)) multiplexer_32 (
    .in0(p), .in1(la), .in2(lb), .in3(lc), .in4(ld), .in5(le), .in6(lf), .in7(lg), .in8(lh), .in9(li),
    .in10(lj), .in11(lk), .in12(ll), .in13(lm), .in14(ln), .in15(lo), .out(multiplexer_2_out[15]), .sel(amt));
  Multiplexer #(.select(4)) multiplexer_33 (
    .in0(1'b0), .in1(a), .in2(b), .in3(c), .in4(d), .in5(e), .in6(f), .in7(g), .in8(h), .in9(i), .in10(j),
    .in11(k), .in12(l), .in13(m), .in14(n), .in15(o), .out(multiplexer_33_out), .sel(amt));

  // Other names for the same wires on the sheet: x[3:0] = amt
endmodule

module reverse16 (
  input  [15:0] Input_bus_1,
  output [15:0] Output_bus_1
);


  assign Output_bus_1 = {Input_bus_1[0], Input_bus_1[1], Input_bus_1[2], Input_bus_1[3], Input_bus_1[4], Input_bus_1[5], Input_bus_1[6], Input_bus_1[7], Input_bus_1[8], Input_bus_1[9], Input_bus_1[10], Input_bus_1[11], Input_bus_1[12], Input_bus_1[13], Input_bus_1[14], Input_bus_1[15]};
endmodule

module dataFlags (
  input  [15:0] data,
  output odd,
  output nz,
  output zero,
  output neg
);

  nor nor_1 (zero, data[0], data[1], data[2], data[3], data[4], data[5], data[6], data[7], data[8], data[9], data[10], data[11], data[12], data[13], data[14], data[15]);
  not not_1 (nz, zero);

  assign neg = data[15];
  assign odd = data[0];
endmodule

module highestSetBit (
  input  [15:0] data,
  output [15:0] hsb
);

  wire [15:0] multiplexer_1_out, multiplexer_2_out, multiplexer_3_out, multiplexer_4_out, multiplexer_5_out,
       multiplexer_6_out, multiplexer_7_out, multiplexer_8_out, multiplexer_9_out, multiplexer_10_out,
       multiplexer_11_out, multiplexer_12_out, multiplexer_13_out, multiplexer_14_out, multiplexer_15_out;

  Multiplexer #(.width(16)) multiplexer_1 (.in0({16{1'b0}}), .in1(16'h1), .out(multiplexer_1_out), .sel(data[0]));
  Multiplexer #(.width(16)) multiplexer_2 (
    .in0(multiplexer_1_out), .in1(16'h2), .out(multiplexer_2_out), .sel(data[1]));
  Multiplexer #(.width(16)) multiplexer_3 (
    .in0(multiplexer_2_out), .in1(16'h4), .out(multiplexer_3_out), .sel(data[2]));
  Multiplexer #(.width(16)) multiplexer_4 (
    .in0(multiplexer_3_out), .in1(16'h8), .out(multiplexer_4_out), .sel(data[3]));
  Multiplexer #(.width(16)) multiplexer_5 (
    .in0(multiplexer_4_out), .in1(16'h10), .out(multiplexer_5_out), .sel(data[4]));
  Multiplexer #(.width(16)) multiplexer_6 (
    .in0(multiplexer_5_out), .in1(16'h20), .out(multiplexer_6_out), .sel(data[5]));
  Multiplexer #(.width(16)) multiplexer_7 (
    .in0(multiplexer_6_out), .in1(16'h40), .out(multiplexer_7_out), .sel(data[6]));
  Multiplexer #(.width(16)) multiplexer_8 (
    .in0(multiplexer_7_out), .in1(16'h80), .out(multiplexer_8_out), .sel(data[7]));
  Multiplexer #(.width(16)) multiplexer_9 (
    .in0(multiplexer_8_out), .in1(16'h100), .out(multiplexer_9_out), .sel(data[8]));
  Multiplexer #(.width(16)) multiplexer_10 (
    .in0(multiplexer_9_out), .in1(16'h200), .out(multiplexer_10_out), .sel(data[9]));
  Multiplexer #(.width(16)) multiplexer_11 (
    .in0(multiplexer_10_out), .in1(16'h400), .out(multiplexer_11_out), .sel(data[10]));
  Multiplexer #(.width(16)) multiplexer_12 (
    .in0(multiplexer_11_out), .in1(16'h800), .out(multiplexer_12_out), .sel(data[11]));
  Multiplexer #(.width(16)) multiplexer_13 (
    .in0(multiplexer_12_out), .in1(16'h1000), .out(multiplexer_13_out), .sel(data[12]));
  Multiplexer #(.width(16)) multiplexer_14 (
    .in0(multiplexer_13_out), .in1(16'h2000), .out(multiplexer_14_out), .sel(data[13]));
  Multiplexer #(.width(16)) multiplexer_15 (
    .in0(multiplexer_14_out), .in1(16'h4000), .out(multiplexer_15_out), .sel(data[14]));
  Multiplexer #(.width(16)) multiplexer_16 (.in0(multiplexer_15_out), .in1(16'h8000), .out(hsb), .sel(data[15]));
endmodule

module freezeReg (
  input  D,
  input  freeze,
  input  we,
  input  clk,
  input  R,
  output Q
);

  wire multiplexer_1_out;

  Register #(.width(1)) register_1 (.D(multiplexer_1_out), .en(we), .clk(clk), .Q(Q), .clr(R));
  Multiplexer multiplexer_1 (.in0(D), .in1(Q), .out(multiplexer_1_out), .sel(freeze));

  // Notes on the sheet:
  //   we: pull=up
endmodule

module freezeReg4 (
  input  [3:0] D,
  input  freeze,
  input  WE,
  input  clk,
  input  R,
  output [3:0] Q
);

  wire [3:0] multiplexer_1_out;

  Register #(.width(4)) register_1 (.D(multiplexer_1_out), .en(WE), .clk(clk), .Q(Q), .clr(R));
  Multiplexer #(.width(4)) multiplexer_1 (.in0(D), .in1(Q), .out(multiplexer_1_out), .sel(freeze));
endmodule

module freezeReg9 (
  input  [8:0] D,
  input  freeze,
  input  WE,
  input  clk,
  input  R,
  output [8:0] Q
);

  wire [8:0] multiplexer_1_out;

  Register #(.width(9)) register_1 (.D(multiplexer_1_out), .en(WE), .clk(clk), .Q(Q), .clr(R));
  Multiplexer #(.width(9)) multiplexer_1 (.in0(D), .in1(Q), .out(multiplexer_1_out), .sel(freeze));
endmodule

module freezeReg16 (
  input  [15:0] D,
  input  freeze,
  input  WE,
  input  clk,
  input  R,
  output [15:0] Q
);

  wire [15:0] multiplexer_1_out;

  Register #(.width(16)) register_1 (.D(multiplexer_1_out), .en(WE), .clk(clk), .Q(Q), .clr(R));
  Multiplexer #(.width(16)) multiplexer_1 (.in0(D), .in1(Q), .out(multiplexer_1_out), .sel(freeze));
endmodule

module checkMask16 (
  input  [15:0] mask,
  input  [15:0] value,
  input  [15:0] targVal,
  input  prot,
  output valid
);

  wire nor_1_out;
  wire [15:0] and_1_out, xor_1_out;

  assign and_1_out = mask & value;  // AND_Gate and_1, 16 bits wide
  assign xor_1_out = and_1_out ^ targVal;  // XOR_Gate xor_1, 16 bits wide
  nor nor_1 (nor_1_out, xor_1_out[0], xor_1_out[1], xor_1_out[2], xor_1_out[3], xor_1_out[4], xor_1_out[5], xor_1_out[6], xor_1_out[7], xor_1_out[8], xor_1_out[9], xor_1_out[10], xor_1_out[11], xor_1_out[12], xor_1_out[13], xor_1_out[14], xor_1_out[15]);
  or or_1 (valid, nor_1_out, ~prot);  // OR_Gate
endmodule

module checkMask4 (
  input  [3:0] mask,
  input  [3:0] value,
  input  [3:0] targVal,
  input  prot,
  output valid
);

  wire nor_1_out;
  wire [3:0] and_1_out, xor_1_out;

  assign and_1_out = mask & value;  // AND_Gate and_1, 4 bits wide
  assign xor_1_out = and_1_out ^ targVal;  // XOR_Gate xor_1, 4 bits wide
  nor nor_1 (nor_1_out, xor_1_out[0], xor_1_out[1], xor_1_out[2], xor_1_out[3]);
  or or_1 (valid, nor_1_out, ~prot);  // OR_Gate
endmodule

module PC_Handler (
  input  [15:0] Fetch_In,
  input  clk,
  input  F,
  input  R,
  input  [15:0] Fetch_Addr,
  input  [15:0] Expected_Addr,
  output [15:0] Fetch_Out,
  output Override
);

  wire or_1_out;
  wire [15:0] F_Loc_Cache_q, Fetch_Cache_q, xor_1_out;

  freezeReg16 Fetch_Cache (.freeze(F), .D(Fetch_In), .WE(1'b1), .clk(clk), .R(R), .Q(Fetch_Cache_q));
  freezeReg16 F_Loc_Cache (.freeze(F), .D(Fetch_Addr), .WE(1'b1), .clk(clk), .R(R), .Q(F_Loc_Cache_q));
  Multiplexer #(.width(16)) multiplexer_1 (.in0(Fetch_Cache_q), .in1({16{1'b0}}), .out(Fetch_Out), .sel(or_1_out));
  assign xor_1_out = F_Loc_Cache_q ^ Expected_Addr;  // XOR_Gate xor_1, 16 bits wide
  or or_1 (or_1_out, xor_1_out[0], xor_1_out[1], xor_1_out[2], xor_1_out[3], xor_1_out[4], xor_1_out[5], xor_1_out[6], xor_1_out[7], xor_1_out[8], xor_1_out[9], xor_1_out[10], xor_1_out[11], xor_1_out[12], xor_1_out[13], xor_1_out[14], xor_1_out[15]);
  not not_1 (Override, or_1_out);
endmodule

module PC_Pred (
  input  [15:0] Fetch_In,
  input  [15:0] Fetch_Addr,
  output [15:0] Fetch_Addr_Out
);

  Adder #(.width(16)) adder_1 (.a({16{1'b0}}), .b(Fetch_Addr), .out(Fetch_Addr_Out), .cin(1'b1));  // open: cout
endmodule
