// Logisim project Multipliers.circ as structural Verilog: 10 circuits, main circuit FA
module FA (
  input  a,
  input  b,
  input  cin,
  output cout,
  output s
);

  FAopt1 faopt1_1 (.a(a), .b(b), .cin(cin), .s(s), .cout(cout));
endmodule

module uMull8 (
  input  [7:0] A,
  input  [7:0] B,
  output [15:0] AB
);

  wire fa_2_cout, fa_2_s, fa_3_cout, fa_3_s, fa_5_cout, fa_5_s, fa_6_cout, fa_6_s, fa_7_cout, fa_7_s,
       fa_9_cout, fa_9_s, fa_10_cout, fa_10_s, fa_11_cout, fa_11_s, fa_12_cout, fa_12_s, fa_13_cout, fa_13_s,
       fa_14_cout, fa_14_s, fa_16_cout, fa_16_s, fa_17_cout, fa_17_s, fa_18_cout, fa_18_s, fa_20_cout,
       fa_20_s, fa_21_cout, fa_21_s, fa_22_cout, fa_22_s, fa_23_cout, fa_23_s, fa_24_cout, fa_24_s,
       fa_26_cout, fa_26_s, fa_27_cout, fa_27_s, fa_28_cout, fa_28_s, fa_29_cout, fa_29_s, fa_31_cout,
       fa_31_s, fa_32_cout, fa_32_s, fa_33_cout, fa_33_s, fa_34_cout, fa_34_s, fa_36_cout, fa_36_s,
       fa_37_cout, fa_37_s, fa_38_cout, fa_38_s, fa_39_cout, fa_39_s, fa_40_cout, fa_40_s, fa_42_cout,
       fa_42_s, fa_43_cout, fa_43_s, fa_44_cout, fa_44_s, fa_45_cout, fa_45_s, fa_47_cout, fa_47_s,
       fa_48_cout, fa_48_s, fa_49_cout, fa_49_s, fa_51_cout, fa_51_s, fa_52_cout, fa_52_s, fa_53_cout,
       fa_54_cout, fa_54_s, fa_55_cout, fa_56_cout;
  wire [7:0] r0, r1, r2, r3, r4, r5, r6, r7;
  wire [15:0] undriven;
  wire [15:1] fa_56_s;

  and and_1 (r0[7], B[0], A[7]);
  and and_2 (r1[7], B[1], A[7]);
  and and_3 (r2[7], B[2], A[7]);
  and and_4 (r3[7], B[3], A[7]);
  and and_5 (r4[7], B[4], A[7]);
  and and_6 (r5[7], B[5], A[7]);
  and and_7 (r6[7], B[6], A[7]);
  and and_8 (r7[7], B[7], A[7]);
  and and_9 (r0[6], B[0], A[6]);
  and and_10 (r1[6], B[1], A[6]);
  and and_11 (r2[6], B[2], A[6]);
  and and_12 (r3[6], B[3], A[6]);
  and and_13 (r4[6], B[4], A[6]);
  and and_14 (r5[6], B[5], A[6]);
  and and_15 (r6[6], B[6], A[6]);
  and and_16 (r7[6], B[7], A[6]);
  and and_17 (r0[5], B[0], A[5]);
  and and_18 (r1[5], B[1], A[5]);
  and and_19 (r2[5], B[2], A[5]);
  and and_20 (r3[5], B[3], A[5]);
  and and_21 (r4[5], B[4], A[5]);
  and and_22 (r5[5], B[5], A[5]);
  and and_23 (r6[5], B[6], A[5]);
  and and_24 (r7[5], B[7], A[5]);
  and and_25 (r0[4], B[0], A[4]);
  and and_26 (r1[4], B[1], A[4]);
  and and_27 (r2[4], B[2], A[4]);
  and and_28 (r3[4], B[3], A[4]);
  and and_29 (r4[4], B[4], A[4]);
  and and_30 (r5[4], B[5], A[4]);
  and and_31 (r6[4], B[6], A[4]);
  and and_32 (r7[4], B[7], A[4]);
  and and_33 (r0[3], B[0], A[3]);
  and and_34 (r1[3], B[1], A[3]);
  and and_35 (r2[3], B[2], A[3]);
  and and_36 (r3[3], B[3], A[3]);
  and and_37 (r4[3], B[4], A[3]);
  and and_38 (r5[3], B[5], A[3]);
  and and_39 (r6[3], B[6], A[3]);
  and and_40 (r7[3], B[7], A[3]);
  and and_41 (r0[2], B[0], A[2]);
  and and_42 (r1[2], B[1], A[2]);
  and and_43 (r2[2], B[2], A[2]);
  and and_44 (r3[2], B[3], A[2]);
  and and_45 (r4[2], B[4], A[2]);
  and and_46 (r5[2], B[5], A[2]);
  and and_47 (r6[2], B[6], A[2]);
  and and_48 (r7[2], B[7], A[2]);
  and and_49 (r0[1], B[0], A[1]);
  and and_50 (r1[1], B[1], A[1]);
  and and_51 (r2[1], B[2], A[1]);
  and and_52 (r3[1], B[3], A[1]);
  and and_53 (r4[1], B[4], A[1]);
  and and_54 (r5[1], B[5], A[1]);
  and and_55 (r6[1], B[6], A[1]);
  and and_56 (r7[1], B[7], A[1]);
  and and_57 (r0[0], B[0], A[0]);
  and and_58 (r1[0], B[1], A[0]);
  and and_59 (r2[0], B[2], A[0]);
  and and_60 (r3[0], B[3], A[0]);
  and and_61 (r4[0], B[4], A[0]);
  and and_62 (r5[0], B[5], A[0]);
  and and_63 (r6[0], B[6], A[0]);
  and and_64 (r7[0], B[7], A[0]);
  FA fa_1 (.a(fa_3_cout), .b(fa_2_cout), .cin(r7[7]), .s(undriven[14]), .cout(fa_56_s[15]));
  FA fa_2 (.a(fa_5_cout), .b(r7[6]), .cin(r6[7]), .s(fa_2_s), .cout(fa_2_cout));
  FA fa_3 (.a(fa_6_cout), .b(fa_2_s), .s(fa_3_s), .cout(fa_3_cout));  // open: cin
  FA fa_4 (.a(fa_7_cout), .b(fa_3_s), .s(undriven[13]), .cout(fa_56_s[14]));  // open: cin
  FA fa_5 (.a(r7[5]), .b(r6[6]), .cin(r5[7]), .s(fa_5_s), .cout(fa_5_cout));
  FA fa_6 (.a(fa_9_cout), .b(fa_5_s), .s(fa_6_s), .cout(fa_6_cout));  // open: cin
  FA fa_7 (.a(fa_10_cout), .b(fa_6_s), .s(fa_7_s), .cout(fa_7_cout));  // open: cin
  FA fa_8 (.a(fa_14_cout), .b(fa_7_s), .s(undriven[12]), .cout(fa_56_s[13]));  // open: cin
  FA fa_9 (.a(r6[5]), .b(r5[6]), .cin(r4[7]), .s(fa_9_s), .cout(fa_9_cout));
  FA fa_10 (.a(fa_11_cout), .b(r7[4]), .cin(fa_9_s), .s(fa_10_s), .cout(fa_10_cout));
  FA fa_11 (.a(r4[6]), .b(r3[7]), .s(fa_11_s), .cout(fa_11_cout));  // open: cin
  FA fa_12 (.a(r7[3]), .b(r6[4]), .cin(r5[5]), .s(fa_12_s), .cout(fa_12_cout));
  FA fa_13 (.a(fa_16_cout), .b(fa_12_s), .cin(fa_11_s), .s(fa_13_s), .cout(fa_13_cout));
  FA fa_14 (.a(fa_13_cout), .b(fa_12_cout), .cin(fa_10_s), .s(fa_14_s), .cout(fa_14_cout));
  FA fa_15 (.a(fa_18_cout), .b(fa_14_s), .s(fa_56_s[11]), .cout(fa_56_s[12]));  // open: cin
  FA fa_16 (.a(r4[5]), .b(r3[6]), .cin(r2[7]), .s(fa_16_s), .cout(fa_16_cout));
  FA fa_17 (.a(r7[2]), .b(r6[3]), .cin(r5[4]), .s(fa_17_s), .cout(fa_17_cout));
  FA fa_18 (.a(fa_22_cout), .b(fa_17_cout), .cin(fa_13_s), .s(fa_18_s), .cout(fa_18_cout));
  FA fa_19 (.a(fa_24_cout), .b(fa_18_s), .s(fa_56_s[10]), .cout(undriven[11]));  // open: cin
  FA fa_20 (.a(r3[5]), .b(r2[6]), .cin(r1[7]), .s(fa_20_s), .cout(fa_20_cout));
  FA fa_21 (.a(r6[2]), .b(r5[3]), .cin(r4[4]), .s(fa_21_s), .cout(fa_21_cout));
  FA fa_22 (.a(fa_20_cout), .b(fa_17_s), .cin(fa_16_s), .s(fa_22_s), .cout(fa_22_cout));
  FA fa_23 (.a(fa_21_s), .b(fa_20_s), .s(fa_23_s), .cout(fa_23_cout));  // open: cin
  FA fa_24 (.a(fa_23_cout), .b(fa_21_cout), .cin(fa_22_s), .s(fa_24_s), .cout(fa_24_cout));
  FA fa_25 (.a(fa_29_cout), .b(fa_28_cout), .cin(fa_24_s), .s(fa_56_s[9]), .cout(undriven[10]));
  FA fa_26 (.a(r2[5]), .b(r1[6]), .cin(r0[7]), .s(fa_26_s), .cout(fa_26_cout));
  FA fa_27 (.a(r5[2]), .b(r4[3]), .cin(r3[4]), .s(fa_27_s), .cout(fa_27_cout));
  FA fa_28 (.a(fa_27_cout), .b(fa_26_cout), .cin(r7[1]), .s(fa_28_s), .cout(fa_28_cout));
  FA fa_29 (.a(fa_32_cout), .b(fa_28_s), .cin(fa_23_s), .s(fa_29_s), .cout(fa_29_cout));
  FA fa_30 (.a(fa_34_cout), .b(fa_33_cout), .cin(fa_29_s), .s(fa_56_s[8]), .cout(undriven[9]));
  FA fa_31 (.a(r2[4]), .b(r1[5]), .cin(r0[6]), .s(fa_31_s), .cout(fa_31_cout));
  FA fa_32 (.a(r6[1]), .b(fa_27_s), .cin(fa_26_s), .s(fa_32_s), .cout(fa_32_cout));
  FA fa_33 (.a(fa_36_cout), .b(fa_31_cout), .cin(r7[0]), .s(fa_33_s), .cout(fa_33_cout));
  FA fa_34 (.a(fa_38_cout), .b(fa_33_s), .cin(fa_32_s), .s(fa_34_s), .cout(fa_34_cout));
  FA fa_35 (.a(fa_40_cout), .b(fa_39_cout), .cin(fa_34_s), .s(fa_56_s[7]), .cout(undriven[8]));
  FA fa_36 (.a(r5[1]), .b(r4[2]), .cin(r3[3]), .s(fa_36_s), .cout(fa_36_cout));
  FA fa_37 (.a(r2[3]), .b(r1[4]), .cin(r0[5]), .s(fa_37_s), .cout(fa_37_cout));
  FA fa_38 (.a(fa_36_s), .b(fa_31_s), .s(fa_38_s), .cout(fa_38_cout));  // open: cin
  FA fa_39 (.a(fa_42_cout), .b(fa_37_cout), .cin(r6[0]), .s(fa_39_s), .cout(fa_39_cout));
  FA fa_40 (.a(fa_44_cout), .b(fa_39_s), .cin(fa_38_s), .s(fa_40_s), .cout(fa_40_cout));
  FA fa_41 (.a(fa_45_cout), .b(fa_40_s), .s(fa_56_s[6]), .cout(undriven[7]));  // open: cin
  FA fa_42 (.a(r5[0]), .b(r4[1]), .cin(r3[2]), .s(fa_42_s), .cout(fa_42_cout));
  FA fa_43 (.a(r1[3]), .b(r0[4]), .s(fa_43_s), .cout(fa_43_cout));  // open: cin
  FA fa_44 (.a(fa_43_cout), .b(fa_42_s), .cin(fa_37_s), .s(fa_44_s), .cout(fa_44_cout));
  FA fa_45 (.a(fa_48_cout), .b(fa_47_cout), .cin(fa_44_s), .s(fa_45_s), .cout(fa_45_cout));
  FA fa_46 (.a(fa_49_cout), .b(fa_45_s), .s(fa_56_s[5]), .cout(undriven[6]));  // open: cin
  FA fa_47 (.a(r4[0]), .b(r3[1]), .cin(r2[2]), .s(fa_47_s), .cout(fa_47_cout));
  FA fa_48 (.a(fa_51_cout), .b(fa_47_s), .cin(fa_43_s), .s(fa_48_s), .cout(fa_48_cout));
  FA fa_49 (.a(fa_52_cout), .b(fa_48_s), .s(fa_49_s), .cout(fa_49_cout));  // open: cin
  FA fa_50 (.a(fa_53_cout), .b(fa_49_s), .s(undriven[4]), .cout(undriven[5]));  // open: cin
  FA fa_51 (.a(r2[1]), .b(r1[2]), .cin(r0[3]), .s(fa_51_s), .cout(fa_51_cout));
  FA fa_52 (.a(fa_54_cout), .b(r3[0]), .cin(fa_51_s), .s(fa_52_s), .cout(fa_52_cout));
  FA fa_53 (.a(fa_55_cout), .b(fa_52_s), .s(fa_56_s[3]), .cout(fa_53_cout));  // open: cin
  FA fa_54 (.a(r2[0]), .b(r1[1]), .cin(r0[2]), .s(fa_54_s), .cout(fa_54_cout));
  FA fa_55 (.a(fa_56_cout), .b(fa_54_s), .s(fa_56_s[2]), .cout(fa_55_cout));  // open: cin
  FA fa_56 (.a(r1[0]), .b(r0[1]), .s(fa_56_s[1]), .cout(fa_56_cout));  // open: cin
  logisim16A_S logisim16a_s_1 (.a({fa_56_s, r0[0]}), .b(undriven), .s(AB));  // open: OP, overflow
endmodule

module uMull16 (
  input  [15:0] A,
  input  [15:0] B,
  output [15:0] AB,
  output Overflow
);

  wire and_1_out, logisim16a_s_1_overflow, logisim16a_s_2_overflow, or_1_out, or_2_out, or_3_out, or_4_out,
       or_5_out, or_6_out, or_7_out;
  wire [7:0] undriven, undriven_2;
  wire [15:0] logisim16a_s_1_s, umull8_1_ab, umull8_2_ab, umull8_3_ab;

  uMull8 umull8_1 (.A(A[7:0]), .B(B[7:0]), .AB(umull8_1_ab));
  uMull8 umull8_2 (.A(A[15:8]), .B(B[7:0]), .AB(umull8_2_ab));
  uMull8 umull8_3 (.A(A[7:0]), .B(B[15:8]), .AB(umull8_3_ab));
  or or_1 (or_1_out, A[8], A[9], A[10], A[11], A[12], A[13], A[14], A[15]);
  or or_2 (or_2_out, B[8], B[9], B[10], B[11], B[12], B[13], B[14], B[15]);
  and and_1 (and_1_out, or_1_out, or_2_out);
  or or_3 (or_3_out, umull8_2_ab[8], umull8_2_ab[9], umull8_2_ab[10], umull8_2_ab[11], umull8_2_ab[12], umull8_2_ab[13], umull8_2_ab[14], umull8_2_ab[15]);
  logisim16A_S logisim16a_s_1 (
    .a(umull8_1_ab), .b({umull8_2_ab[7:0], undriven}), .s(logisim16a_s_1_s),
    .overflow(logisim16a_s_1_overflow));  // open: OP
  or or_4 (or_4_out, logisim16a_s_1_overflow, or_3_out);
  logisim16A_S logisim16a_s_2 (
    .a(logisim16a_s_1_s), .b({umull8_3_ab[7:0], undriven_2}), .s(AB), .overflow(logisim16a_s_2_overflow));  // open: OP
  or or_5 (or_5_out, umull8_3_ab[8], umull8_3_ab[9], umull8_3_ab[10], umull8_3_ab[11], umull8_3_ab[12], umull8_3_ab[13], umull8_3_ab[14], umull8_3_ab[15]);
  or or_6 (or_6_out, or_4_out, or_5_out);
  or or_7 (or_7_out, logisim16a_s_2_overflow, or_6_out);
  or or_8 (Overflow, or_7_out, and_1_out);
endmodule

module SetSign (
  input  [15:0] A,
  input  S,
  output [15:0] U
);

  wire [14:0] negator_1_out;

  Negator #(.width(15)) negator_1 (.in(A[14:0]), .out(negator_1_out));
  Multiplexer #(.width(15)) multiplexer_1 (.in0(A[14:0]), .in1(negator_1_out), .out(U[14:0]), .sel(S));

  assign U[15] = S;
endmodule

module GetSign (
  input  [15:0] A,
  output [15:0] U,
  output S
);

  wire [14:0] negator_1_out;

  Negator #(.width(15)) negator_1 (.in(A[14:0]), .out(negator_1_out));
  Multiplexer #(.width(15)) multiplexer_1 (.in0(A[14:0]), .in1(negator_1_out), .out(U[14:0]), .sel(A[15]));

  assign S = A[15];
  assign U[15] = 1'b0;
endmodule

module mul16 (
  input  [15:0] A,
  input  [15:0] B,
  input  s,
  output [15:0] AB,
  output O
);

  wire getsign_1_s, getsign_2_s, xor_1_out;
  wire [15:0] getsign_1_u, getsign_2_u, multiplexer_1_out, multiplexer_2_out, setsign_1_u, umull16_1_ab;

  GetSign getsign_1 (.A(A), .U(getsign_1_u), .S(getsign_1_s));
  GetSign getsign_2 (.A(B), .U(getsign_2_u), .S(getsign_2_s));
  Multiplexer #(.width(16)) multiplexer_1 (.in0(A), .in1(getsign_1_u), .out(multiplexer_1_out), .sel(s));
  uMull16 umull16_1 (.A(multiplexer_1_out), .B(multiplexer_2_out), .Overflow(O), .AB(umull16_1_ab));
  Multiplexer #(.width(16)) multiplexer_2 (.in0(B), .in1(getsign_2_u), .out(multiplexer_2_out), .sel(s));
  xor xor_1 (xor_1_out, getsign_1_s, getsign_2_s);
  SetSign setsign_1 (.A(umull16_1_ab), .S(xor_1_out), .U(setsign_1_u));
  Multiplexer #(.width(16)) multiplexer_3 (.in0(umull16_1_ab), .in1(setsign_1_u), .out(AB), .sel(s));
endmodule

module uDiv16 (
  input  [15:0] A,
  input  [15:0] B,
  output [15:0] R,
  output [15:0] D
);

  wire [15:0] csub2_1_c, csub_1_c, csub_2_c, csub_3_c, csub_4_c, csub_5_c, csub_6_c, csub_7_c, csub_8_c,
       csub_9_c, csub_10_c, csub_11_c, csub_12_c, csub_13_c, csub_14_c, shiftadd_1_c, shiftadd_2_c,
       shiftadd_3_c, shiftadd_4_c, shiftadd_5_c, shiftadd_6_c, shiftadd_7_c, shiftadd_8_c, shiftadd_9_c,
       shiftadd_10_c, shiftadd_11_c, shiftadd_12_c, shiftadd_13_c, shiftadd_14_c, shiftadd_15_c,
       shiftadd_16_c;

  ShiftAdd shiftadd_1 (.A({16{1'b0}}), .B(A[15]), .C(shiftadd_1_c));
  CSub2 csub2_1 (.A(shiftadd_1_c), .B(B), .C(csub2_1_c), .D(D[15]));
  ShiftAdd shiftadd_2 (.A(csub2_1_c), .B(A[14]), .C(shiftadd_2_c));
  CSub csub_1 (.B(B), .A(shiftadd_2_c), .C(csub_1_c), .D(D[14]));
  ShiftAdd shiftadd_3 (.A(csub_1_c), .B(A[13]), .C(shiftadd_3_c));
  CSub csub_2 (.B(B), .A(shiftadd_3_c), .C(csub_2_c), .D(D[13]));
  ShiftAdd shiftadd_4 (.A(csub_2_c), .B(A[12]), .C(shiftadd_4_c));
  CSub csub_3 (.B(B), .A(shiftadd_4_c), .C(csub_3_c), .D(D[12]));
  ShiftAdd shiftadd_5 (.A(csub_3_c), .B(A[11]), .C(shiftadd_5_c));
  CSub csub_4 (.B(B), .A(shiftadd_5_c), .C(csub_4_c), .D(D[11]));
  ShiftAdd shiftadd_6 (.A(csub_4_c), .B(A[10]), .C(shiftadd_6_c));
  CSub csub_5 (.B(B), .A(shiftadd_6_c), .C(csub_5_c), .D(D[10]));
  ShiftAdd shiftadd_7 (.A(csub_7_c), .B(A[8]), .C(shiftadd_7_c));
  CSub csub_6 (.B(B), .A(shiftadd_7_c), .C(csub_6_c), .D(D[8]));
  ShiftAdd shiftadd_8 (.A(csub_5_c), .B(A[9]), .C(shiftadd_8_c));
  CSub csub_7 (.B(B), .A(shiftadd_8_c), .C(csub_7_c), .D(D[9]));
  ShiftAdd shiftadd_9 (.A(csub_6_c), .B(A[7]), .C(shiftadd_9_c));
  CSub csub_8 (.B(B), .A(shiftadd_9_c), .C(csub_8_c), .D(D[7]));
  ShiftAdd shiftadd_10 (.A(csub_8_c), .B(A[6]), .C(shiftadd_10_c));
  CSub csub_9 (.B(B), .A(shiftadd_10_c), .C(csub_9_c), .D(D[6]));
  ShiftAdd shiftadd_11 (.A(csub_9_c), .B(A[5]), .C(shiftadd_11_c));
  CSub csub_10 (.B(B), .A(shiftadd_11_c), .C(csub_10_c), .D(D[5]));
  ShiftAdd shiftadd_12 (.A(csub_10_c), .B(A[4]), .C(shiftadd_12_c));
  CSub csub_11 (.B(B), .A(shiftadd_12_c), .C(csub_11_c), .D(D[4]));
  ShiftAdd shiftadd_13 (.A(csub_11_c), .B(A[3]), .C(shiftadd_13_c));
  CSub csub_12 (.B(B), .A(shiftadd_13_c), .C(csub_12_c), .D(D[3]));
  ShiftAdd shiftadd_14 (.A(csub_12_c), .B(A[2]), .C(shiftadd_14_c));
  CSub csub_13 (.B(B), .A(shiftadd_14_c), .C(csub_13_c), .D(D[2]));
  ShiftAdd shiftadd_15 (.A(csub_13_c), .B(A[1]), .C(shiftadd_15_c));
  CSub csub_14 (.B(B), .A(shiftadd_15_c), .C(csub_14_c), .D(D[1]));
  ShiftAdd shiftadd_16 (.A(csub_14_c), .B(A[0]), .C(shiftadd_16_c));
  CSub csub_15 (.B(B), .A(shiftadd_16_c), .C(R), .D(D[0]));
endmodule

module CSub (
  input  [15:0] B,
  input  [15:0] A,
  output [15:0] C,
  output D
);

  wire and_1_out, and_2_out, and_3_out, and_4_out, and_5_out, and_6_out, and_7_out, and_8_out, and_9_out,
       and_10_out, and_11_out, and_12_out, and_13_out, and_14_out, and_15_out, and_16_out, and_17_out,
       and_18_out, and_19_out, and_20_out, and_21_out, and_22_out, and_23_out, and_24_out, and_25_out,
       and_26_out, and_27_out, and_28_out, and_29_out, and_30_out, and_31_out, and_32_out, and_33_out,
       and_34_out, and_35_out, and_36_out, and_37_out, and_38_out, and_39_out, and_40_out, and_41_out,
       and_42_out, and_43_out, and_44_out, and_45_out, and_46_out, and_47_out, and_48_out, or_1_out,
       or_2_out, or_3_out, or_4_out, or_5_out, or_6_out, or_7_out, or_8_out, or_9_out, or_10_out, or_11_out,
       or_12_out, or_13_out, or_14_out, or_15_out, or_16_out, or_17_out, or_18_out, or_19_out, or_20_out,
       or_21_out, or_22_out, or_23_out, or_24_out, or_25_out, or_26_out, or_27_out, or_28_out, or_29_out,
       or_31_out, or_32_out, or_33_out;
  wire [15:0] subtractor_1_out;

  and and_1 (and_1_out, A[15], ~B[15]);  // AND_Gate
  and and_2 (and_2_out, ~A[15], B[15]);  // AND_Gate
  buf or_1 (or_1_out, and_2_out);  // OR_Gate
  and and_3 (and_3_out, and_1_out, ~or_1_out);  // AND_Gate
  and and_4 (and_4_out, A[14], ~B[14]);  // AND_Gate
  and and_5 (and_5_out, A[13], ~B[13]);  // AND_Gate
  and and_6 (and_6_out, ~A[14], B[14]);  // AND_Gate
  and and_7 (and_7_out, ~A[13], B[13]);  // AND_Gate
  or or_2 (or_2_out, and_6_out, or_1_out);
  or or_3 (or_3_out, and_7_out, or_2_out);
  and and_8 (and_8_out, and_4_out, ~or_2_out);  // AND_Gate
  and and_9 (and_9_out, and_5_out, ~or_3_out);  // AND_Gate
  buf or_4 (or_4_out, and_3_out);  // OR_Gate
  or or_5 (or_5_out, and_8_out, or_4_out);
  and and_10 (and_10_out, A[12], ~B[12]);  // AND_Gate
  and and_11 (and_11_out, A[11], ~B[11]);  // AND_Gate
  and and_12 (and_12_out, ~A[12], B[12]);  // AND_Gate
  and and_13 (and_13_out, ~A[11], B[11]);  // AND_Gate
  or or_6 (or_6_out, and_12_out, or_3_out);
  or or_7 (or_7_out, and_13_out, or_6_out);
  and and_14 (and_14_out, and_10_out, ~or_6_out);  // AND_Gate
  and and_15 (and_15_out, and_11_out, ~or_7_out);  // AND_Gate
  or or_8 (or_8_out, and_9_out, or_5_out);
  or or_9 (or_9_out, and_14_out, or_8_out);
  and and_16 (and_16_out, A[10], ~B[10]);  // AND_Gate
  and and_17 (and_17_out, A[9], ~B[9]);  // AND_Gate
  and and_18 (and_18_out, ~A[10], B[10]);  // AND_Gate
  and and_19 (and_19_out, ~A[9], B[9]);  // AND_Gate
  or or_10 (or_10_out, and_18_out, or_7_out);
  or or_11 (or_11_out, and_19_out, or_10_out);
  and and_20 (and_20_out, and_16_out, ~or_10_out);  // AND_Gate
  and and_21 (and_21_out, and_17_out, ~or_11_out);  // AND_Gate
  or or_12 (or_12_out, and_15_out, or_9_out);
  or or_13 (or_13_out, and_20_out, or_12_out);
  Subtractor #(.width(16)) subtractor_1 (.a(A), .b(B), .out(subtractor_1_out));  // open: bin, bout
  and and_22 (and_22_out, A[8], ~B[8]);  // AND_Gate
  and and_23 (and_23_out, A[7], ~B[7]);  // AND_Gate
  and and_24 (and_24_out, ~A[8], B[8]);  // AND_Gate
  and and_25 (and_25_out, ~A[7], B[7]);  // AND_Gate
  or or_14 (or_14_out, and_24_out, or_11_out);
  or or_15 (or_15_out, and_25_out, or_14_out);
  and and_26 (and_26_out, and_22_out, ~or_14_out);  // AND_Gate
  and and_27 (and_27_out, and_23_out, ~or_15_out);  // AND_Gate
  or or_16 (or_16_out, and_21_out, or_13_out);
  or or_17 (or_17_out, and_26_out, or_16_out);
  and and_28 (and_28_out, A[6], ~B[6]);  // AND_Gate
  and and_29 (and_29_out, A[5], ~B[5]);  // AND_Gate
  and and_30 (and_30_out, ~A[6], B[6]);  // AND_Gate
  and and_31 (and_31_out, ~A[5], B[5]);  // AND_Gate
  or or_18 (or_18_out, and_30_out, or_15_out);
  or or_19 (or_19_out, and_31_out, or_18_out);
  and and_32 (and_32_out, and_28_out, ~or_18_out);  // AND_Gate
  and and_33 (and_33_out, and_29_out, ~or_19_out);  // AND_Gate
  or or_20 (or_20_out, and_27_out, or_17_out);
  or or_21 (or_21_out, and_32_out, or_20_out);
  and and_34 (and_34_out, A[4], ~B[4]);  // AND_Gate
  and and_35 (and_35_out, A[3], ~B[3]);  // AND_Gate
  and and_36 (and_36_out, ~A[4], B[4]);  // AND_Gate
  and and_37 (and_37_out, ~A[3], B[3]);  // AND_Gate
  or or_22 (or_22_out, and_36_out, or_19_out);
  or or_23 (or_23_out, and_37_out, or_22_out);
  and and_38 (and_38_out, and_34_out, ~or_22_out);  // AND_Gate
  and and_39 (and_39_out, and_35_out, ~or_23_out);  // AND_Gate
  or or_24 (or_24_out, and_33_out, or_21_out);
  or or_25 (or_25_out, and_38_out, or_24_out);
  and and_40 (and_40_out, A[2], ~B[2]);  // AND_Gate
  and and_41 (and_41_out, A[1], ~B[1]);  // AND_Gate
  and and_42 (and_42_out, ~A[2], B[2]);  // AND_Gate
  and and_43 (and_43_out, ~A[1], B[1]);  // AND_Gate
  or or_26 (or_26_out, and_42_out, or_23_out);
  or or_27 (or_27_out, and_43_out, or_26_out);
  and and_44 (and_44_out, and_40_out, ~or_26_out);  // AND_Gate
  and and_45 (and_45_out, and_41_out, ~or_27_out);  // AND_Gate
  or or_28 (or_28_out, and_39_out, or_25_out);
  or or_29 (or_29_out, and_44_out, or_28_out);
  Multiplexer #(.width(16)) multiplexer_1 (.in0(A), .in1(subtractor_1_out), .out(C), .sel(D));
  and and_46 (and_46_out, A[0], ~B[0]);  // AND_Gate
  or or_30 (D, ~or_31_out, or_33_out);  // OR_Gate
  and and_47 (and_47_out, ~A[0], B[0]);  // AND_Gate
  or or_31 (or_31_out, and_47_out, or_27_out);
  and and_48 (and_48_out, and_46_out, ~or_31_out);  // AND_Gate
  or or_32 (or_32_out, and_45_out, or_29_out);
  or or_33 (or_33_out, and_48_out, or_32_out);
endmodule

module ShiftAdd (
  input  [15:0] A,
  input  B,
  output [15:0] C
);


  assign C = {A[14:0], B};
  // also tied to GND on the sheet: A[15]
endmodule

module CSub2 (
  input  [15:0] A,
  input  [15:0] B,
  output [15:0] C,
  output D
);

  wire [15:0] subtractor_1_out;

  Subtractor #(.width(16)) subtractor_1 (.a(A), .b(B), .out(subtractor_1_out));  // open: bin, bout
  Multiplexer #(.width(16)) multiplexer_1 (.in0(A), .in1(subtractor_1_out), .out(C), .sel(D));
  not not_1 (D, subtractor_1_out[15]);
endmodule
